// Logisim project RC_TTL_MP.circ as structural Verilog
module CPU (
  input  CPU_ENABLE,
  input  [7:0] Data_In,
  input  FORK_LOAD,
  input  [15:0] FORK_ADDR_IN,
  input  [7:0] CPU_ID,
  output [23:0] Sequnce,
  output FREE,
  output [15:0] Adress_Bus,
  output Write_en,
  output [7:0] Data_Out,
  output BUS_REQ,
  output FORK_REQ
);

  wire ALOAD_NEW, ALOAD_OLD, ALU_A, AT_ROW_NEW, AT_ROW_OLD, clock_2_out, COND_CARRY, COND_CARRY_REG,
       COND_SIGN, COND_SIGN_REG, COND_ZERO, COND_ZERO_REG, CPUEN_NEW, fetch_1_incsel, fetch_1_linc,
       fetch_1_linstr, fetch_1_mer, fetch_1_pcload, fetch_1_pcsel, FK_ALOAD, FK_IDOE, FK_MSEL, FK_NEWOP,
       HI_FK, input_register_1_w, instr_decoder_1_goto, instr_decoder_1_in_8, instructions_1_aload,
       instructions_1_bload, instructions_1_j1_load, instructions_1_j2_load, instructions_1_j_sel,
       instructions_1_m1_load, instructions_1_m2_load, keyboard_1_avail, MER_C, mov_16_1_j_load,
       mov_16_1_j_sel, mov_16_1_m_load, mov_16_1_xy_load, mov_16_1_xy_sel, MSEL_NEW, MSEL_OLD, n7404_1_pin2,
       n7404_3_pin2, n7408_1_pin2, n7408_1_pin4, n7408_1_pin6, n7408_1_pin13, n7408_2_pin2, n7408_2_pin3,
       n7408_2_pin6, n7408_2_pin8, n7408_2_pin9, n7408_3_pin8, n7408_4_pin3, n7432_2_pin1, n7432_2_pin2,
       n7432_2_pin3, n7432_2_pin4, n7432_2_pin5, n7432_2_pin6, n7432_2_pin10, n7432_2_pin11, n7432_2_pin13,
       n7432_3_pin8, n7432_3_pin9, n7432_5_pin1, n7432_5_pin3, n7432_6_pin2, n7432_6_pin3, n7432_6_pin5,
       n7432_6_pin8, n7432_6_pin9, n7432_6_pin11, n7432_6_pin13, n7432_7_pin2, n7432_8_pin3, n7432_8_pin4,
       n7432_8_pin6, n7432_8_pin11, n7432_9_pin5, n7432_9_pin8, n7432_9_pin10, n7432_10_pin13, n7432_11_pin3,
       n7432_11_pin6, n7432_12_pin3, n7474_1_pin1, n7474_1_pin2, n7474_1_pin3, n7474_1_pin6, n7474_2_pin1,
       n74245_3_pin1, nFK_IDOE, nFORK_LOAD, PCL_NEW, PCL_OLD, SEQ_AT08, srl_out_1_serial_out,
       srl_out_1_serial_out_xor;
  wire [6:0] keyboard_1_data;
  wire [7:0] Data_Bus, dual_regist_b_c_3_bout, dual_regist_b_c_3_cout, gate_8_1_dout, Instr_Bus,
       instructions_1_dout, instructions_1_reg_load, instructions_1_reg_select;
  wire [15:0] Sequence_extra;

  _7474 #(.ShowInternalStructure("true")) u_7474_1 (
    .pin1(n7474_1_pin1), .pin2(n7474_1_pin2), .pin3(n7474_1_pin3), .pin6(n7474_1_pin6));  // open: pin4, pin5, pin13, pin12, pin11, pin10, pin9, pin8
  _7408 #(.ShowInternalStructure("true")) u_7408_1 (
    .pin1(n7474_1_pin1), .pin2(n7408_1_pin2), .pin3(n7474_1_pin2), .pin4(n7408_1_pin4), .pin5(CPUEN_NEW),
    .pin6(n7408_1_pin6), .pin13(n7408_1_pin13), .pin12(Sequnce[7]), .pin11(n7408_1_pin2),
    .pin10(n7408_1_pin6), .pin9(n7474_1_pin6), .pin8(n7474_1_pin3));
  Button #(.press("passive")) button_1 ();  // open: out
  Clock clock_1 (.out(n7408_1_pin4));
  _7432 #(.ShowInternalStructure("true")) u_7432_1 (
    .pin1(AT_ROW_OLD), .pin2(FK_NEWOP), .pin3(AT_ROW_NEW), .pin4(PCL_OLD), .pin5(FORK_LOAD), .pin6(PCL_NEW),
    .pin13(FK_ALOAD), .pin12(ALOAD_OLD), .pin11(ALOAD_NEW), .pin10(FK_MSEL), .pin9(MSEL_OLD), .pin8(MSEL_NEW));
  _7404 #(.ShowInternalStructure("true")) u_7404_1 (
    .pin1(n7474_1_pin2), .pin2(n7404_1_pin2));  // open: pin3, pin4, pin5, pin6, pin13, pin12, pin11, pin10, pin9, pin8
  _7432 #(.ShowInternalStructure("true")) u_7432_2 (
    .pin1(n7432_2_pin1), .pin2(n7432_2_pin2), .pin3(n7432_2_pin3), .pin4(n7432_2_pin4), .pin5(n7432_2_pin5),
    .pin6(n7432_2_pin6), .pin13(n7432_2_pin13), .pin12(n7432_2_pin3), .pin11(n7432_2_pin11),
    .pin10(n7432_2_pin10), .pin9(n7432_2_pin6), .pin8(AT_ROW_OLD));
  _7432 #(.ShowInternalStructure("true")) u_7432_3 (
    .pin10(n7408_1_pin13), .pin9(n7432_3_pin9), .pin8(n7432_3_pin8));  // open: pin1, pin2, pin3, pin4, pin5, pin6, pin13, pin12, pin11
  SEQUENCER sequencer_1 (
    .CLOCK(n7474_1_pin3), .AT08(n7432_3_pin8), .AT10(AT_ROW_NEW), .AT12(n7432_2_pin11),
    .AT14(instr_decoder_1_in_8), .AT30(instr_decoder_1_goto), .SQC(Sequnce), .SQC_EXTRA(Sequence_extra));  // open: START
  _7432 #(.ShowInternalStructure("true")) u_7432_4 (
    .pin1(CPU_ENABLE), .pin2(FORK_LOAD), .pin3(CPUEN_NEW));  // open: pin4, pin5, pin6, pin13, pin12, pin11, pin10, pin9, pin8
  _7432 #(.ShowInternalStructure("true")) u_7432_5 (
    .pin1(n7432_5_pin1), .pin3(n7432_5_pin3), .pin4(n7432_5_pin3), .pin6(ALU_A));  // open: pin2, pin5, pin13, pin12, pin11, pin10, pin9, pin8
  GATE_8 gate_8_1 (.EN(n7432_2_pin4), .DIn(Instr_Bus), .DOut(gate_8_1_dout));
  _7408 #(.ShowInternalStructure("true")) u_7408_2 (
    .pin1(n7432_2_pin4), .pin2(n7408_2_pin2), .pin3(n7408_2_pin3), .pin4(n7432_5_pin1), .pin5(n7432_2_pin4),
    .pin6(n7408_2_pin6), .pin13(n7474_1_pin3), .pin10(n7432_2_pin5), .pin9(n7408_2_pin9), .pin8(n7408_2_pin8));  // open: pin12, pin11
  _7404 #(.ShowInternalStructure("true")) u_7404_2 (
    .pin1(FORK_LOAD), .pin2(nFORK_LOAD), .pin3(FK_IDOE), .pin4(nFK_IDOE));  // open: pin5, pin6, pin13, pin12, pin11, pin10, pin9, pin8
  ALU alu_1 (
    .BIn(dual_regist_b_c_3_bout), .CIn(dual_regist_b_c_3_cout), .INSTR(gate_8_1_dout), .SQC(Sequnce),
    .A(n7432_5_pin1), .D(n7408_2_pin2), .DOut(Data_Bus), .Sign(COND_SIGN), .Zero(COND_ZERO), .Cry(COND_CARRY));
  Fetch fetch_1 (
    .SQC(Sequnce), .PCSEL(fetch_1_pcsel), .MER(fetch_1_mer), .LINC(fetch_1_linc), .LINSTR(fetch_1_linstr),
    .INCSEL(fetch_1_incsel), .PCLOAD(fetch_1_pcload));
  _7432 #(.ShowInternalStructure("true")) u_7432_6 (
    .pin1(fetch_1_pcsel), .pin2(n7432_6_pin2), .pin3(n7432_6_pin3), .pin4(fetch_1_pcload),
    .pin5(n7432_6_pin5), .pin6(PCL_OLD), .pin13(n7432_6_pin13), .pin12(fetch_1_linc), .pin11(n7432_6_pin11),
    .pin10(fetch_1_incsel), .pin9(n7432_6_pin9), .pin8(n7432_6_pin8));
  _7432 #(.ShowInternalStructure("true")) u_7432_7 (
    .pin1(fetch_1_mer), .pin2(n7432_7_pin2), .pin3(MER_C), .pin4(MER_C), .pin5(Write_en), .pin6(BUS_REQ));  // open: pin13, pin12, pin11, pin10, pin9, pin8
  GATE_8 gate_8_2 (.EN(Write_en), .DIn(Data_Bus), .DOut(Data_Out));
  _74245 #(.ShowInternalStructure("true")) u_74245_1 (
    .pin1(HI_FK), .pin2(FORK_ADDR_IN[0]), .pin3(FORK_ADDR_IN[1]), .pin4(FORK_ADDR_IN[2]),
    .pin5(FORK_ADDR_IN[3]), .pin6(FORK_ADDR_IN[4]), .pin7(FORK_ADDR_IN[5]), .pin8(FORK_ADDR_IN[6]),
    .pin9(FORK_ADDR_IN[7]), .pin19(nFORK_LOAD), .pin18(Adress_Bus[0]), .pin17(Adress_Bus[1]),
    .pin16(Adress_Bus[2]), .pin15(Adress_Bus[3]), .pin14(Adress_Bus[4]), .pin13(Adress_Bus[5]),
    .pin12(Adress_Bus[6]), .pin11(Adress_Bus[7]));
  Incrementer incrementer_1 (
    .CLK(n7474_1_pin3), .LoadINC(n7432_6_pin11), .AIn(Adress_Bus), .SELECTINC(n7432_6_pin8), .AOut(Adress_Bus));
  _7408 #(.ShowInternalStructure("true")) u_7408_3 (
    .pin10(ALU_A), .pin9(n7432_2_pin4), .pin8(n7408_3_pin8));  // open: pin1, pin2, pin3, pin4, pin5, pin6, pin13, pin12, pin11
  INSTRUCTIONS instructions_1 (
    .MOV_8(n7432_3_pin9), .SQC(Sequnce), .INSTR(Instr_Bus), .LOAD_8(n7432_2_pin2),
    .F({COND_SIGN_REG, COND_ZERO_REG, COND_CARRY_REG}), .SAVE_8(n7432_2_pin1), .SET_AB(n7432_2_pin5),
    .GOTO_16(instr_decoder_1_goto), .Sequence_Extra(Sequence_extra), .REG_SELECT(instructions_1_reg_select),
    .REG_LOAD(instructions_1_reg_load), .M_SEL(MSEL_OLD), .PC_SEL(n7432_6_pin2), .MEW(Write_en),
    .MER(n7432_7_pin2), .ALOAD(instructions_1_aload), .BLOAD(instructions_1_bload),
    .DOut(instructions_1_dout), .J1_LOAD(instructions_1_j1_load), .M1_LOAD(instructions_1_m1_load),
    .J2_LOAD(instructions_1_j2_load), .M2_LOAD(instructions_1_m2_load), .INC_LOAD(n7432_6_pin13),
    .J_SEL(instructions_1_j_sel), .PC_LOAD(n7432_6_pin5), .INC_SEL(n7432_6_pin9), .AT_08(SEQ_AT08));  // open: REG_IN
  _7432 #(.ShowInternalStructure("true")) u_7432_8 (
    .pin1(instructions_1_bload), .pin2(instructions_1_reg_load[6]), .pin3(n7432_8_pin3), .pin4(n7432_8_pin4),
    .pin5(instructions_1_aload), .pin6(n7432_8_pin6), .pin13(n7408_2_pin3),
    .pin12(instructions_1_reg_load[4]), .pin11(n7432_8_pin11), .pin10(n7408_2_pin6),
    .pin9(instructions_1_reg_load[7]), .pin8(n7432_8_pin4));
  _7474 #(.ShowInternalStructure("true")) u_7474_2 (
    .pin1(n7474_2_pin1), .pin2(COND_CARRY), .pin3(n7408_3_pin8), .pin5(COND_CARRY_REG), .pin13(n7474_2_pin1),
    .pin12(COND_ZERO), .pin11(n7408_3_pin8), .pin9(COND_ZERO_REG));  // open: pin4, pin6, pin10, pin8
  _7432 #(.ShowInternalStructure("true")) u_7432_9 (
    .pin4(n7432_8_pin6), .pin5(n7432_9_pin5), .pin6(ALOAD_OLD), .pin10(n7432_9_pin10),
    .pin9(instructions_1_reg_select[0]), .pin8(n7432_9_pin8));  // open: pin1, pin2, pin3, pin13, pin12, pin11
  _7404 #(.ShowInternalStructure("true")) u_7404_3 (
    .pin1(n7408_2_pin8), .pin2(n7404_3_pin2), .pin3(MER_C), .pin4(n7408_2_pin9));  // open: pin5, pin6, pin13, pin12, pin11, pin10, pin9, pin8
  Pull_Resistor pull_resistor_1 (.node(instructions_1_reg_load));
  Dual_Regist_B_C dual_regist_b_c_1 (
    .CLK(n7474_1_pin3), .LOAD12(PCL_NEW), .SELECT12(n7432_6_pin3), .D16In(Adress_Bus), .D16Out(Adress_Bus));  // open: DIn, LOAD1, LOAD2, SELECT1, SELECT2, BOut, COut
  _7474 #(.ShowInternalStructure("true")) u_7474_3 (
    .pin1(n7474_2_pin1), .pin2(COND_SIGN), .pin3(n7408_3_pin8), .pin5(COND_SIGN_REG), .pin13(n7474_2_pin1),
    .pin12(n7474_2_pin1), .pin11(n7408_3_pin8));  // open: pin4, pin6, pin10, pin9, pin8
  _74245 #(.ShowInternalStructure("true")) u_74245_2 (
    .pin1(HI_FK), .pin2(FORK_ADDR_IN[8]), .pin3(FORK_ADDR_IN[9]), .pin4(FORK_ADDR_IN[10]),
    .pin5(FORK_ADDR_IN[11]), .pin6(FORK_ADDR_IN[12]), .pin7(FORK_ADDR_IN[13]), .pin8(FORK_ADDR_IN[14]),
    .pin9(FORK_ADDR_IN[15]), .pin19(nFORK_LOAD), .pin18(Adress_Bus[8]), .pin17(Adress_Bus[9]),
    .pin16(Adress_Bus[10]), .pin15(Adress_Bus[11]), .pin14(Adress_Bus[12]), .pin13(Adress_Bus[13]),
    .pin12(Adress_Bus[14]), .pin11(Adress_Bus[15]));
  Pull_Resistor pull_resistor_2 (.node(instructions_1_reg_select));
  GATE_8_ALU gate_8_alu_1 (.EN(MER_C), .DIn(Data_In), .DOut(Data_Bus));
  Dual_Regist_B_C dual_regist_b_c_2 (
    .DIn(Data_Bus), .CLK(n7474_1_pin3), .LOAD1(fetch_1_linstr), .BOut(Instr_Bus));  // open: LOAD2, SELECT1, SELECT2, LOAD12, SELECT12, D16In, COut, D16Out
  _74245 #(.ShowInternalStructure("true")) u_74245_3 (
    .pin1(n74245_3_pin1), .pin2(instructions_1_dout[0]), .pin3(instructions_1_dout[1]),
    .pin4(instructions_1_dout[2]), .pin5(instructions_1_dout[3]), .pin6(instructions_1_dout[4]),
    .pin7(instructions_1_dout[5]), .pin8(instructions_1_dout[6]), .pin9(instructions_1_dout[7]),
    .pin19(n7404_3_pin2), .pin18(Data_Bus[0]), .pin17(Data_Bus[1]), .pin16(Data_Bus[2]), .pin15(Data_Bus[3]),
    .pin14(Data_Bus[4]), .pin13(Data_Bus[5]), .pin12(Data_Bus[6]), .pin11(Data_Bus[7]));
  _7432 #(.ShowInternalStructure("true")) u_7432_10 (
    .pin13(n7432_10_pin13), .pin12(n7432_2_pin10), .pin11(n7408_1_pin13));  // open: pin1, pin2, pin3, pin4, pin5, pin6, pin10, pin9, pin8
  Instr_Decoder instr_decoder_1 (
    .in_1(Instr_Bus), .setab(n7432_2_pin5), .mov8(n7432_3_pin9), .goto(instr_decoder_1_goto),
    .alu(n7432_2_pin4), .load(n7432_2_pin2), .store(n7432_2_pin1), .mov16(n7432_2_pin13),
    .OUT_8(n7432_2_pin10), .HALT(n7432_10_pin13), .IN_8(instr_decoder_1_in_8));  // open: inc
  Dual_Register dual_register_1 (
    .DIn(Data_Bus), .CLK(n7474_1_pin3), .LOAD1(ALOAD_NEW), .LOAD2(n7432_8_pin11), .SELECT1(n7432_9_pin8),
    .SELECT2(instructions_1_reg_select[3]), .DOut(Data_Bus));  // open: LOAD12, SELECT12, D16In, D16Out
  Dual_Regist_B_C dual_regist_b_c_3 (
    .DIn(Data_Bus), .CLK(n7474_1_pin3), .LOAD1(n7432_8_pin3), .LOAD2(instructions_1_reg_load[5]),
    .SELECT1(instructions_1_reg_select[1]), .SELECT2(instructions_1_reg_select[2]),
    .BOut(dual_regist_b_c_3_bout), .COut(dual_regist_b_c_3_cout));  // open: LOAD12, SELECT12, D16In, D16Out
  Keyboard keyboard_1 (
    .clk(n7408_4_pin3), .re(input_register_1_w), .avail(keyboard_1_avail), .data(keyboard_1_data));  // open: clr
  _74245 #(.ShowInternalStructure("true")) u_74245_4 (
    .pin1(HI_FK), .pin2(CPU_ID[7]), .pin3(CPU_ID[6]), .pin4(CPU_ID[5]), .pin5(CPU_ID[4]), .pin6(CPU_ID[3]),
    .pin7(CPU_ID[2]), .pin8(CPU_ID[1]), .pin9(CPU_ID[0]), .pin19(nFK_IDOE), .pin18(Data_Bus[0]),
    .pin17(Data_Bus[1]), .pin16(Data_Bus[2]), .pin15(Data_Bus[3]), .pin14(Data_Bus[4]), .pin13(Data_Bus[5]),
    .pin12(Data_Bus[6]), .pin11(Data_Bus[7]));
  _7432 #(.ShowInternalStructure("true")) u_7432_11 (
    .pin1(instructions_1_m1_load), .pin2(instructions_1_reg_load[1]), .pin3(n7432_11_pin3),
    .pin4(instructions_1_m2_load), .pin5(instructions_1_reg_load[0]), .pin6(n7432_11_pin6));  // open: pin13, pin12, pin11, pin10, pin9, pin8
  _7408 #(.ShowInternalStructure("true")) u_7408_4 (
    .pin1(instr_decoder_1_in_8), .pin2(n7474_1_pin3), .pin3(n7408_4_pin3));  // open: pin4, pin5, pin6, pin13, pin12, pin11, pin10, pin9, pin8
  Dual_Register XY_Register (
    .DIn(Data_Bus), .CLK(n7474_1_pin3), .LOAD1(instructions_1_reg_load[3]),
    .LOAD2(instructions_1_reg_load[2]), .SELECT1(instructions_1_reg_select[4]),
    .SELECT2(instructions_1_reg_select[5]), .LOAD12(mov_16_1_xy_load), .SELECT12(mov_16_1_xy_sel),
    .D16In(Adress_Bus), .DOut(Data_Bus), .D16Out(Adress_Bus));
  Dual_Register M_Register (
    .DIn(Data_Bus), .CLK(n7474_1_pin3), .LOAD1(n7432_11_pin3), .LOAD2(n7432_11_pin6),
    .SELECT1(instructions_1_reg_select[6]), .SELECT2(instructions_1_reg_select[7]), .LOAD12(mov_16_1_m_load),
    .SELECT12(MSEL_NEW), .D16In(Adress_Bus), .DOut(Data_Bus), .D16Out(Adress_Bus));
  Dual_Register J_Register (
    .DIn(Data_Bus), .CLK(n7474_1_pin3), .LOAD1(instructions_1_j1_load), .LOAD2(instructions_1_j2_load),
    .LOAD12(mov_16_1_j_load), .SELECT12(n7432_12_pin3), .D16Out(Adress_Bus));  // open: SELECT1, SELECT2, D16In, DOut
  Input_register input_register_1 (
    .CLK(n7408_4_pin3), .Load(keyboard_1_avail), .Data_In({1'b0, keyboard_1_data}), .SQC(Sequnce),
    .En(instr_decoder_1_in_8), .Data_Out(Data_Bus), .Reg_A(n7432_9_pin5), .W(input_register_1_w));  // open: Clock
  MOV_16 mov_16_1 (
    .Instructions(Instr_Bus), .SQC(Sequnce), .M_LOAD(mov_16_1_m_load), .J_LOAD(mov_16_1_j_load),
    .XY_LOAD(mov_16_1_xy_load), .J_SEL(mov_16_1_j_sel), .XY_SEL(mov_16_1_xy_sel));
  _7432 #(.ShowInternalStructure("true")) u_7432_12 (
    .pin1(instructions_1_j_sel), .pin2(mov_16_1_j_sel), .pin3(n7432_12_pin3));  // open: pin4, pin5, pin6, pin13, pin12, pin11, pin10, pin9, pin8
  Clock clock_2 (.out(clock_2_out));
  FORKUNIT forkunit_1 (
    .INSTR(Instr_Bus), .SQC(Sequnce), .NEWOP(FK_NEWOP), .ID_ALOAD(FK_ALOAD), .ID_OE(FK_IDOE),
    .FORK_REQ(FORK_REQ), .FORK_MSEL(FK_MSEL));
  SRL_OUT srl_out_1 (
    .DATA(Data_Bus), .ENABLE(n7432_2_pin10), .CLK(clock_2_out), .SQC(Sequnce),
    .Serial_Out_XOR(srl_out_1_serial_out_xor), .Serial_out(srl_out_1_serial_out), .Resume(n7474_1_pin1),
    .A_SELECT(n7432_9_pin10));
  STATUS_CHECK status_check_1 (.SQC(Sequnce), .INSTR(Instr_Bus), .FREE(FREE));
  // Digital_Oscilloscope #(.nState(14)) digital_oscilloscope_1: pin names not known; wires that end beside it: clock_2_out, srl_out_1_serial_out_xor, srl_out_1_serial_out
  // also tied to VCC on the sheet: {n7474_2_pin1, n74245_3_pin1, HI_FK}

  // Other names for the same wires on the sheet: AB0 = Adress_Bus[0]; AB1 = Adress_Bus[1]; AB2 = Adress_Bus[2];
  //   AB3 = Adress_Bus[3]; AB4 = Adress_Bus[4]; AB5 = Adress_Bus[5]; AB6 = Adress_Bus[6]; AB7 = Adress_Bus[7];
  //   AB8 = Adress_Bus[8]; AB9 = Adress_Bus[9]; AB10 = Adress_Bus[10]; AB11 = Adress_Bus[11]; AB12 = Adress_Bus[12];
  //   AB13 = Adress_Bus[13]; AB14 = Adress_Bus[14]; AB15 = Adress_Bus[15]; BUS_REQ_N = BUS_REQ; CID7 = CPU_ID[0];
  //   CID6 = CPU_ID[1]; CID5 = CPU_ID[2]; CID4 = CPU_ID[3]; CID3 = CPU_ID[4]; CID2 = CPU_ID[5]; CID1 = CPU_ID[6];
  //   CID0 = CPU_ID[7]; CPUEN_OLD = CPU_ENABLE; DBB0 = Data_Bus[0]; DBB1 = Data_Bus[1]; DBB2 = Data_Bus[2];
  //   DBB3 = Data_Bus[3]; DBB4 = Data_Bus[4]; DBB5 = Data_Bus[5]; DBB6 = Data_Bus[6]; DBB7 = Data_Bus[7];
  //   FK_REQ = FORK_REQ; FI0 = FORK_ADDR_IN[0]; FI1 = FORK_ADDR_IN[1]; FI2 = FORK_ADDR_IN[2]; FI3 = FORK_ADDR_IN[3];
  //   FI4 = FORK_ADDR_IN[4]; FI5 = FORK_ADDR_IN[5]; FI6 = FORK_ADDR_IN[6]; FI7 = FORK_ADDR_IN[7];
  //   FI8 = FORK_ADDR_IN[8]; FI9 = FORK_ADDR_IN[9]; FI10 = FORK_ADDR_IN[10]; FI11 = FORK_ADDR_IN[11];
  //   FI12 = FORK_ADDR_IN[12]; FI13 = FORK_ADDR_IN[13]; FI14 = FORK_ADDR_IN[14]; FI15 = FORK_ADDR_IN[15];
  //   MEW_C = Write_en; Sequence[23:0] = Sequnce
endmodule

module SEQUENCER (
  input  START,
  input  CLOCK,
  input  AT08,
  input  AT10,
  input  AT12,
  input  AT14,
  input  AT30,
  output [23:0] SQC,
  output [15:0] SQC_EXTRA
);

  wire n7404_1_pin1, n7404_1_pin2, n7404_1_pin3, n7404_1_pin4, n7404_1_pin6, n7404_1_pin8, n7404_1_pin9,
       n7404_1_pin10, n7404_1_pin11, n7404_1_pin12, n7404_1_pin13, n7432_1_pin3, n7432_1_pin6, n7432_1_pin8,
       n7432_1_pin11, n7432_2_pin4, n7432_2_pin5, n7432_2_pin6, n7432_3_pin3, n7432_3_pin6, n7432_3_pin8,
       n7432_3_pin12, n7432_3_pin13, n7432_4_pin1, n7432_4_pin2, n7432_4_pin4, n7432_4_pin5, n7432_4_pin9,
       n7432_4_pin11, n7432_5_pin1, n7432_5_pin2, n7432_5_pin3, n7432_5_pin5, n7432_5_pin6, n7432_5_pin11,
       n7432_5_pin12, n7432_5_pin13, n7432_6_pin3, n7432_6_pin11, n7432_7_pin3, n7432_7_pin8, n7432_7_pin11,
       n7432_8_pin3, n7432_8_pin6, n7432_8_pin8, n7432_8_pin11, n7432_9_pin3, n7432_9_pin6, n7432_9_pin8,
       n7432_9_pin11, n7432_10_pin1, n7432_10_pin3, n7432_10_pin6, n7432_10_pin11, n7432_11_pin3,
       n7432_11_pin6, n7432_11_pin11;

  _7432 #(.ShowInternalStructure("true")) u_7432_1 (
    .pin1(SQC[7]), .pin2(SQC[6]), .pin3(n7432_1_pin3), .pin4(SQC[5]), .pin5(SQC[4]), .pin6(n7432_1_pin6),
    .pin13(SQC[3]), .pin12(SQC[2]), .pin11(n7432_1_pin11), .pin10(SQC[1]), .pin9(SQC[0]), .pin8(n7432_1_pin8));
  _7432 #(.ShowInternalStructure("true")) u_7432_2 (
    .pin4(n7432_2_pin4), .pin5(n7432_2_pin5), .pin6(n7432_2_pin6));  // open: pin1, pin2, pin3, pin13, pin12, pin11, pin10, pin9, pin8
  _7432 #(.ShowInternalStructure("true")) u_7432_3 (
    .pin1(n7432_1_pin3), .pin2(n7432_1_pin6), .pin3(n7432_3_pin3), .pin4(n7432_3_pin3), .pin5(n7432_1_pin11),
    .pin6(n7432_3_pin6), .pin13(n7432_3_pin13), .pin12(n7432_3_pin12), .pin11(n7432_2_pin5),
    .pin10(n7432_1_pin8), .pin9(n7432_3_pin6), .pin8(n7432_3_pin8));
  _7432 #(.ShowInternalStructure("true")) u_7432_4 (
    .pin1(n7432_4_pin1), .pin2(n7432_4_pin2), .pin3(n7432_3_pin13), .pin4(n7432_4_pin4), .pin5(n7432_4_pin5),
    .pin6(n7432_4_pin2), .pin12(SQC_EXTRA[15]), .pin11(n7432_4_pin11), .pin10(n7432_4_pin11),
    .pin9(n7432_4_pin9), .pin8(n7432_4_pin4));  // open: pin13
  _7404 #(.ShowInternalStructure("true")) u_7404_1 (
    .pin1(n7404_1_pin1), .pin2(n7404_1_pin2), .pin3(n7404_1_pin3), .pin4(n7404_1_pin4), .pin5(n7432_3_pin8),
    .pin6(n7404_1_pin6), .pin13(n7404_1_pin13), .pin12(n7404_1_pin12), .pin11(n7404_1_pin11),
    .pin10(n7404_1_pin10), .pin9(n7404_1_pin9), .pin8(n7404_1_pin8));
  _7432 #(.ShowInternalStructure("true")) u_7432_5 (
    .pin1(n7432_5_pin1), .pin2(n7432_5_pin2), .pin3(n7432_5_pin3), .pin4(n7432_5_pin3), .pin5(n7432_5_pin5),
    .pin6(n7432_5_pin6), .pin13(n7432_5_pin13), .pin12(n7432_5_pin12), .pin11(n7432_5_pin11),
    .pin10(n7432_5_pin11), .pin9(n7432_5_pin6), .pin8(n7404_1_pin9));
  _74273 #(.ShowInternalStructure("true")) u_74273_1 (
    .pin1(n7404_1_pin8), .pin2(SQC[0]), .pin3(n7432_2_pin6), .pin4(SQC[0]), .pin5(SQC[1]), .pin6(SQC[2]),
    .pin7(SQC[1]), .pin8(SQC[2]), .pin9(SQC[3]), .pin19(SQC[7]), .pin18(SQC[6]), .pin17(SQC[5]),
    .pin16(SQC[6]), .pin15(SQC[5]), .pin14(SQC[4]), .pin13(SQC[3]), .pin12(SQC[4]), .pin11(CLOCK));
  _7408 #(.ShowInternalStructure("true")) u_7408_1 (
    .pin1(SQC[14]), .pin2(AT14), .pin3(n7432_5_pin13), .pin4(AT12), .pin5(SQC[12]), .pin6(n7432_5_pin5),
    .pin13(AT08), .pin12(SQC[8]), .pin11(n7432_5_pin2), .pin10(SQC[10]), .pin9(AT10), .pin8(n7432_5_pin1));
  _7408 #(.ShowInternalStructure("true")) u_7408_2 (
    .pin1(AT14), .pin2(n7404_1_pin10), .pin3(n7432_3_pin12), .pin4(AT12), .pin5(n7404_1_pin2),
    .pin6(n7432_4_pin1), .pin13(AT08), .pin12(n7404_1_pin6), .pin11(n7432_4_pin9), .pin10(AT10),
    .pin9(n7404_1_pin4), .pin8(n7432_4_pin5));
  _74273 #(.ShowInternalStructure("true")) u_74273_2 (
    .pin1(n7404_1_pin8), .pin2(SQC[8]), .pin3(SQC[7]), .pin4(SQC[8]), .pin5(SQC[9]), .pin6(SQC[10]),
    .pin7(SQC[9]), .pin8(SQC[10]), .pin9(SQC[11]), .pin19(SQC[15]), .pin18(SQC[14]), .pin17(SQC[13]),
    .pin16(SQC[14]), .pin15(SQC[13]), .pin14(SQC[12]), .pin13(SQC[11]), .pin12(SQC[12]), .pin11(CLOCK));
  _7432 #(.ShowInternalStructure("true")) u_7432_6 (
    .pin1(n7404_1_pin3), .pin2(SQC[10]), .pin3(n7432_6_pin3), .pin4(n7432_6_pin3), .pin5(SQC[11]),
    .pin6(n7404_1_pin1), .pin13(SQC[8]), .pin12(SQC[9]), .pin11(n7432_6_pin11), .pin10(n7432_6_pin11),
    .pin9(n7432_3_pin8), .pin8(n7404_1_pin3));
  _7408 #(.ShowInternalStructure("true")) u_7408_3 (
    .pin1(AT30), .pin2(SQC_EXTRA[6]), .pin3(n7432_5_pin12), .pin4(n7404_1_pin12), .pin5(AT30),
    .pin6(n7432_2_pin4));  // open: pin13, pin12, pin11, pin10, pin9, pin8
  _74273 #(.ShowInternalStructure("true")) u_74273_3 (
    .pin1(n7404_1_pin8), .pin2(SQC[16]), .pin3(SQC[15]), .pin4(SQC[16]), .pin5(SQC[17]), .pin6(SQC[18]),
    .pin7(SQC[17]), .pin8(SQC[18]), .pin9(SQC[19]), .pin19(SQC[23]), .pin18(SQC[22]), .pin17(SQC[21]),
    .pin16(SQC[22]), .pin15(SQC[21]), .pin14(SQC[20]), .pin13(SQC[19]), .pin12(SQC[20]), .pin11(CLOCK));
  _74273 #(.ShowInternalStructure("true")) u_74273_4 (
    .pin1(n7404_1_pin8), .pin2(SQC_EXTRA[0]), .pin3(SQC[23]), .pin4(SQC_EXTRA[0]), .pin5(SQC_EXTRA[1]),
    .pin6(SQC_EXTRA[2]), .pin7(SQC_EXTRA[1]), .pin8(SQC_EXTRA[2]), .pin9(SQC_EXTRA[3]), .pin19(SQC_EXTRA[7]),
    .pin18(SQC_EXTRA[6]), .pin17(SQC_EXTRA[5]), .pin16(SQC_EXTRA[6]), .pin15(SQC_EXTRA[5]),
    .pin14(SQC_EXTRA[4]), .pin13(SQC_EXTRA[3]), .pin12(SQC_EXTRA[4]), .pin11(CLOCK));
  _7432 #(.ShowInternalStructure("true")) u_7432_7 (
    .pin1(n7404_1_pin1), .pin2(SQC[12]), .pin3(n7432_7_pin3), .pin4(n7432_7_pin3), .pin5(SQC[13]),
    .pin6(n7404_1_pin11), .pin13(SQC[14]), .pin12(n7404_1_pin11), .pin11(n7432_7_pin11),
    .pin10(n7432_7_pin11), .pin9(SQC[15]), .pin8(n7432_7_pin8));
  _74273 #(.ShowInternalStructure("true")) u_74273_5 (
    .pin1(n7404_1_pin8), .pin2(SQC_EXTRA[8]), .pin3(SQC_EXTRA[7]), .pin4(SQC_EXTRA[8]), .pin5(SQC_EXTRA[9]),
    .pin6(SQC_EXTRA[10]), .pin7(SQC_EXTRA[9]), .pin8(SQC_EXTRA[10]), .pin9(SQC_EXTRA[11]),
    .pin19(SQC_EXTRA[15]), .pin18(SQC_EXTRA[14]), .pin17(SQC_EXTRA[13]), .pin16(SQC_EXTRA[14]),
    .pin15(SQC_EXTRA[13]), .pin14(SQC_EXTRA[12]), .pin13(SQC_EXTRA[11]), .pin12(SQC_EXTRA[12]), .pin11(CLOCK));
  _7432 #(.ShowInternalStructure("true")) u_7432_8 (
    .pin1(n7432_7_pin8), .pin2(SQC[16]), .pin3(n7432_8_pin3), .pin4(n7432_8_pin3), .pin5(SQC[19]),
    .pin6(n7432_8_pin6), .pin13(n7432_8_pin6), .pin12(SQC[17]), .pin11(n7432_8_pin11), .pin10(n7432_8_pin11),
    .pin9(SQC[18]), .pin8(n7432_8_pin8));
  _7432 #(.ShowInternalStructure("true")) u_7432_9 (
    .pin1(SQC_EXTRA[0]), .pin2(SQC_EXTRA[1]), .pin3(n7432_9_pin3), .pin4(n7432_9_pin3), .pin5(SQC_EXTRA[2]),
    .pin6(n7432_9_pin6), .pin13(n7432_9_pin6), .pin12(SQC_EXTRA[3]), .pin11(n7432_9_pin11),
    .pin10(n7432_9_pin11), .pin9(SQC_EXTRA[4]), .pin8(n7432_9_pin8));
  _7432 #(.ShowInternalStructure("true")) u_7432_10 (
    .pin1(n7432_10_pin1), .pin2(SQC[21]), .pin3(n7432_10_pin3), .pin4(n7432_10_pin3), .pin5(SQC[23]),
    .pin6(n7432_10_pin6), .pin13(n7432_8_pin8), .pin12(SQC[20]), .pin11(n7432_10_pin11),
    .pin10(n7432_10_pin11), .pin9(SQC[22]), .pin8(n7432_10_pin1));
  _7432 #(.ShowInternalStructure("true")) u_7432_11 (
    .pin1(SQC_EXTRA[5]), .pin2(n7432_9_pin8), .pin3(n7432_11_pin3), .pin4(n7432_11_pin3),
    .pin6(n7432_11_pin6), .pin13(n7432_11_pin6), .pin12(n7432_10_pin6), .pin11(n7432_11_pin11),
    .pin10(n7432_11_pin11), .pin8(n7404_1_pin13));  // open: pin5, pin9
endmodule

// ALU
module ALU1 (
  input  [7:0] BIn,
  input  CarryIn,
  input  [7:0] CIn,
  output CarryOut,
  output [7:0] SumOut
);

  wire n7408_1_pin3, n7408_1_pin6, n7408_1_pin8, n7408_1_pin11, n7408_3_pin3, n7408_3_pin6, n7408_3_pin8,
       n7408_3_pin11, n7432_1_pin4, n7432_1_pin5, n7432_1_pin6, n7432_1_pin8, n7432_1_pin9, n7432_1_pin10,
       n7432_1_pin11, n7432_2_pin4, n7432_2_pin5, n7432_2_pin8, n7432_2_pin9, n7432_2_pin10, n7432_2_pin11,
       n7486_1_pin3, n7486_1_pin9, n7486_1_pin11, n7486_2_pin3, n7486_2_pin11, n7486_3_pin3, n7486_3_pin9,
       n7486_3_pin11, n7486_4_pin3, n7486_4_pin11;

  _7486 #(.ShowInternalStructure("true")) u_7486_1 (
    .pin1(BIn[7]), .pin2(CIn[0]), .pin3(n7486_1_pin3), .pin4(n7486_1_pin3), .pin5(CarryIn), .pin6(SumOut[0]),
    .pin13(BIn[6]), .pin12(CIn[1]), .pin11(n7486_1_pin11), .pin10(n7486_1_pin11), .pin9(n7486_1_pin9),
    .pin8(SumOut[1]));
  _7408 #(.ShowInternalStructure("true")) u_7408_1 (
    .pin1(BIn[7]), .pin2(CIn[0]), .pin3(n7408_1_pin3), .pin4(n7486_1_pin3), .pin5(CarryIn),
    .pin6(n7408_1_pin6), .pin13(CIn[1]), .pin12(BIn[6]), .pin11(n7408_1_pin11), .pin10(n7486_1_pin11),
    .pin9(n7486_1_pin9), .pin8(n7408_1_pin8));
  _7432 #(.ShowInternalStructure("true")) u_7432_1 (
    .pin1(n7408_1_pin3), .pin2(n7408_1_pin6), .pin3(n7486_1_pin9), .pin4(n7432_1_pin4), .pin5(n7432_1_pin5),
    .pin6(n7432_1_pin6), .pin13(n7408_1_pin11), .pin12(n7408_1_pin8), .pin11(n7432_1_pin11),
    .pin10(n7432_1_pin10), .pin9(n7432_1_pin9), .pin8(n7432_1_pin8));
  _7486 #(.ShowInternalStructure("true")) u_7486_2 (
    .pin1(BIn[5]), .pin2(CIn[2]), .pin3(n7486_2_pin3), .pin4(n7486_2_pin3), .pin5(n7432_1_pin11),
    .pin6(SumOut[2]), .pin13(BIn[4]), .pin12(CIn[3]), .pin11(n7486_2_pin11), .pin10(n7486_2_pin11),
    .pin9(n7432_1_pin8), .pin8(SumOut[3]));
  _7408 #(.ShowInternalStructure("true")) u_7408_2 (
    .pin1(CIn[2]), .pin2(BIn[5]), .pin3(n7432_1_pin10), .pin4(n7486_2_pin3), .pin5(n7432_1_pin11),
    .pin6(n7432_1_pin9), .pin13(CIn[3]), .pin12(BIn[4]), .pin11(n7432_1_pin4), .pin10(n7432_1_pin8),
    .pin9(n7486_2_pin11), .pin8(n7432_1_pin5));
  _7486 #(.ShowInternalStructure("true")) u_7486_3 (
    .pin1(BIn[3]), .pin2(CIn[4]), .pin3(n7486_3_pin3), .pin4(n7486_3_pin3), .pin5(n7432_1_pin6),
    .pin6(SumOut[4]), .pin13(BIn[2]), .pin12(CIn[5]), .pin11(n7486_3_pin11), .pin10(n7486_3_pin11),
    .pin9(n7486_3_pin9), .pin8(SumOut[5]));
  _7408 #(.ShowInternalStructure("true")) u_7408_3 (
    .pin1(BIn[3]), .pin2(CIn[4]), .pin3(n7408_3_pin3), .pin4(n7486_3_pin3), .pin5(n7432_1_pin6),
    .pin6(n7408_3_pin6), .pin13(CIn[5]), .pin12(BIn[2]), .pin11(n7408_3_pin11), .pin10(n7486_3_pin11),
    .pin9(n7486_3_pin9), .pin8(n7408_3_pin8));
  _7432 #(.ShowInternalStructure("true")) u_7432_2 (
    .pin1(n7408_3_pin3), .pin2(n7408_3_pin6), .pin3(n7486_3_pin9), .pin4(n7432_2_pin4), .pin5(n7432_2_pin5),
    .pin6(CarryOut), .pin13(n7408_3_pin11), .pin12(n7408_3_pin8), .pin11(n7432_2_pin11),
    .pin10(n7432_2_pin10), .pin9(n7432_2_pin9), .pin8(n7432_2_pin8));
  _7486 #(.ShowInternalStructure("true")) u_7486_4 (
    .pin1(BIn[1]), .pin2(CIn[6]), .pin3(n7486_4_pin3), .pin4(n7486_4_pin3), .pin5(n7432_2_pin11),
    .pin6(SumOut[6]), .pin13(BIn[0]), .pin12(CIn[7]), .pin11(n7486_4_pin11), .pin10(n7486_4_pin11),
    .pin9(n7432_2_pin8), .pin8(SumOut[7]));
  _7408 #(.ShowInternalStructure("true")) u_7408_4 (
    .pin1(CIn[6]), .pin2(BIn[1]), .pin3(n7432_2_pin10), .pin4(n7486_4_pin3), .pin5(n7432_2_pin11),
    .pin6(n7432_2_pin9), .pin13(CIn[7]), .pin12(BIn[0]), .pin11(n7432_2_pin4), .pin10(n7432_2_pin8),
    .pin9(n7486_4_pin11), .pin8(n7432_2_pin5));
endmodule

// ALU
module ALU2 (
  input  [7:0] CIn,
  input  [7:0] BIn,
  input  UND,
  input  ODER,
  input  XODER,
  input  NICHT,
  output [7:0] SumOut
);

  wire n7404_1_pin2, n7404_1_pin8, n7404_1_pin10, n7404_1_pin12, n7432_1_pin3, n7432_1_pin6, n7432_1_pin8,
       n7432_1_pin11, n7486_1_pin3, n7486_1_pin6, n7486_1_pin8, n7486_1_pin11, n74245_1_pin11,
       n74245_1_pin12, n74245_1_pin13, n74245_1_pin14, n74245_1_pin15, n74245_1_pin16, n74245_1_pin17,
       n74245_1_pin18, n74245_2_pin11, n74245_2_pin12, n74245_2_pin13, n74245_2_pin14, n74245_3_pin11,
       n74245_3_pin12, n74245_3_pin13, n74245_3_pin14, n74245_4_pin11, n74245_4_pin12, n74245_4_pin13,
       n74245_4_pin14, n74245_4_pin15, n74245_4_pin16, n74245_4_pin17, n74245_4_pin18;

  _7404 #(.ShowInternalStructure("true")) u_7404_1 (
    .pin1(NICHT), .pin2(n7404_1_pin2), .pin13(UND), .pin12(n7404_1_pin12), .pin11(ODER),
    .pin10(n7404_1_pin10), .pin9(XODER), .pin8(n7404_1_pin8));  // open: pin3, pin4, pin5, pin6
  _74245 #(.ShowInternalStructure("true")) u_74245_1 (
    .pin2(SumOut[0]), .pin3(SumOut[1]), .pin4(SumOut[2]), .pin5(SumOut[3]), .pin6(SumOut[4]),
    .pin7(SumOut[5]), .pin8(SumOut[6]), .pin9(SumOut[7]), .pin19(n7404_1_pin12), .pin18(n74245_1_pin18),
    .pin17(n74245_1_pin17), .pin16(n74245_1_pin16), .pin15(n74245_1_pin15), .pin14(n74245_1_pin14),
    .pin13(n74245_1_pin13), .pin12(n74245_1_pin12), .pin11(n74245_1_pin11));  // open: pin1
  _7408 #(.ShowInternalStructure("true")) u_7408_1 (
    .pin1(CIn[7]), .pin2(BIn[0]), .pin3(n74245_1_pin18), .pin4(CIn[6]), .pin5(BIn[1]), .pin6(n74245_1_pin17),
    .pin13(CIn[5]), .pin12(BIn[2]), .pin11(n74245_1_pin16), .pin10(BIn[3]), .pin8(n74245_1_pin15));  // open: pin9
  _7408 #(.ShowInternalStructure("true")) u_7408_2 (
    .pin1(CIn[3]), .pin2(BIn[4]), .pin3(n74245_1_pin14), .pin4(CIn[2]), .pin5(BIn[5]), .pin6(n74245_1_pin13),
    .pin13(CIn[1]), .pin12(BIn[6]), .pin11(n74245_1_pin12), .pin10(CIn[0]), .pin9(BIn[7]),
    .pin8(n74245_1_pin11));
  Pull_Resistor pull_resistor_1 (.node(SumOut));
  _7432 #(.ShowInternalStructure("true")) u_7432_1 (
    .pin1(CIn[7]), .pin2(BIn[0]), .pin3(n7432_1_pin3), .pin4(CIn[6]), .pin5(BIn[1]), .pin6(n7432_1_pin6),
    .pin13(CIn[5]), .pin12(BIn[2]), .pin11(n7432_1_pin11), .pin10(CIn[4]), .pin9(BIn[3]), .pin8(n7432_1_pin8));
  _74245 #(.ShowInternalStructure("true")) u_74245_2 (
    .pin2(SumOut[0]), .pin3(SumOut[1]), .pin4(SumOut[2]), .pin5(SumOut[3]), .pin6(SumOut[4]),
    .pin7(SumOut[5]), .pin8(SumOut[6]), .pin9(SumOut[7]), .pin19(n7404_1_pin10), .pin18(n7432_1_pin3),
    .pin17(n7432_1_pin6), .pin16(n7432_1_pin11), .pin15(n7432_1_pin8), .pin14(n74245_2_pin14),
    .pin13(n74245_2_pin13), .pin12(n74245_2_pin12), .pin11(n74245_2_pin11));  // open: pin1
  _7432 #(.ShowInternalStructure("true")) u_7432_2 (
    .pin1(CIn[3]), .pin2(BIn[4]), .pin3(n74245_2_pin14), .pin4(CIn[2]), .pin5(BIn[5]), .pin6(n74245_2_pin13),
    .pin13(CIn[1]), .pin12(BIn[6]), .pin11(n74245_2_pin12), .pin10(CIn[0]), .pin9(BIn[7]),
    .pin8(n74245_2_pin11));
  _7486 #(.ShowInternalStructure("true")) u_7486_1 (
    .pin1(CIn[7]), .pin2(BIn[0]), .pin3(n7486_1_pin3), .pin4(CIn[6]), .pin5(BIn[1]), .pin6(n7486_1_pin6),
    .pin13(CIn[5]), .pin12(BIn[2]), .pin11(n7486_1_pin11), .pin10(CIn[4]), .pin9(BIn[3]), .pin8(n7486_1_pin8));
  _74245 #(.ShowInternalStructure("true")) u_74245_3 (
    .pin2(SumOut[0]), .pin3(SumOut[1]), .pin4(SumOut[2]), .pin5(SumOut[3]), .pin6(SumOut[4]),
    .pin7(SumOut[5]), .pin8(SumOut[6]), .pin9(SumOut[7]), .pin19(n7404_1_pin8), .pin18(n7486_1_pin3),
    .pin17(n7486_1_pin6), .pin16(n7486_1_pin11), .pin15(n7486_1_pin8), .pin14(n74245_3_pin14),
    .pin13(n74245_3_pin13), .pin12(n74245_3_pin12), .pin11(n74245_3_pin11));  // open: pin1
  _7486 #(.ShowInternalStructure("true")) u_7486_2 (
    .pin1(CIn[3]), .pin2(BIn[4]), .pin3(n74245_3_pin14), .pin4(CIn[2]), .pin5(BIn[5]), .pin6(n74245_3_pin13),
    .pin13(CIn[1]), .pin12(BIn[6]), .pin11(n74245_3_pin12), .pin10(CIn[0]), .pin9(BIn[7]),
    .pin8(n74245_3_pin11));
  _74245 #(.ShowInternalStructure("true")) u_74245_4 (
    .pin2(SumOut[0]), .pin3(SumOut[1]), .pin4(SumOut[2]), .pin5(SumOut[3]), .pin6(SumOut[4]),
    .pin7(SumOut[5]), .pin8(SumOut[6]), .pin9(SumOut[7]), .pin19(n7404_1_pin2), .pin18(n74245_4_pin18),
    .pin17(n74245_4_pin17), .pin16(n74245_4_pin16), .pin15(n74245_4_pin15), .pin14(n74245_4_pin14),
    .pin13(n74245_4_pin13), .pin12(n74245_4_pin12), .pin11(n74245_4_pin11));  // open: pin1
  _7404 #(.ShowInternalStructure("true")) u_7404_2 (
    .pin1(BIn[0]), .pin2(n74245_4_pin18), .pin3(BIn[1]), .pin4(n74245_4_pin17), .pin5(BIn[2]),
    .pin6(n74245_4_pin16), .pin13(BIn[3]), .pin12(n74245_4_pin15), .pin11(BIn[4]), .pin10(n74245_4_pin14),
    .pin9(BIn[5]), .pin8(n74245_4_pin13));
  _7404 #(.ShowInternalStructure("true")) u_7404_3 (
    .pin1(BIn[6]), .pin2(n74245_4_pin12), .pin3(BIn[7]), .pin4(n74245_4_pin11));  // open: pin5, pin6, pin13, pin12, pin11, pin10, pin9, pin8
endmodule

module ALU (
  input  [7:0] BIn,
  input  [7:0] CIn,
  input  [7:0] INSTR,
  input  [23:0] SQC,
  output A,
  output D,
  output [7:0] DOut,
  output Sign,
  output Zero,
  output Cry
);

  wire n7404_1_pin2, n7404_1_pin4, n7404_1_pin6, n7404_1_pin8, n7404_2_pin2, n7404_2_pin4, n7404_2_pin8,
       n7404_2_pin10, n7404_2_pin12, n7404_3_pin5, n7408_1_pin2, n7408_1_pin11, n7408_1_pin12, n7408_2_pin3,
       n7408_2_pin12, n7432_1_pin3, n7432_1_pin9, n7432_1_pin10, n7432_1_pin11, n7432_1_pin12, n7432_1_pin13,
       n7432_2_pin3, n7432_2_pin6, n7432_2_pin11, n7432_3_pin3, n7432_3_pin6, n7432_3_pin11, n7432_3_pin12,
       n7432_4_pin3, n7432_4_pin6, n7432_4_pin12, n74245_1_pin1, n74245_6_pin1, pull_resistor_2_node,
       pull_resistor_3_node, threetoeight_1_o_000, threetoeight_1_o_011, threetoeight_1_o_100,
       threetoeight_1_o_101, threetoeight_1_o_110, threetoeight_1_o_111;
  wire [2:0] n7408_1_pin8;
  wire [7:0] alu1_1_sumout, alu1_2_sumout, alu2_1_sumout, alu2_2_sumout, pull_resistor_1_node;
  wire [7:1] n74245_1_pin17;

  _7408 #(.ShowInternalStructure("true")) u_7408_1 (
    .pin1(INSTR[1]), .pin2(n7408_1_pin2), .pin3(n7408_1_pin8[1]), .pin4(INSTR[2]), .pin5(n7408_1_pin2),
    .pin6(n7408_1_pin8[2]), .pin13(n7408_1_pin2), .pin12(n7408_1_pin12), .pin11(n7408_1_pin11),
    .pin10(n7408_1_pin2), .pin9(INSTR[0]), .pin8(n7408_1_pin8[0]));
  _7404 #(.ShowInternalStructure("true")) u_7404_1 (
    .pin1(n7408_1_pin11), .pin2(n7404_1_pin2), .pin3(n7408_1_pin8[0]), .pin4(n7404_1_pin4),
    .pin5(n7408_1_pin8[1]), .pin6(n7404_1_pin6), .pin9(n7408_1_pin8[2]), .pin8(n7404_1_pin8));  // open: pin13, pin12, pin11, pin10
  _7432 #(.ShowInternalStructure("true")) u_7432_1 (
    .pin1(SQC[7]), .pin2(SQC[8]), .pin3(n7432_1_pin3), .pin4(n7432_1_pin3), .pin5(SQC[9]),
    .pin6(n7408_1_pin2), .pin13(n7432_1_pin13), .pin12(n7432_1_pin12), .pin11(n7432_1_pin11),
    .pin10(n7432_1_pin10), .pin9(n7432_1_pin9), .pin8(n7432_1_pin12));
  _7408 #(.ShowInternalStructure("true")) u_7408_2 (
    .pin1(n7404_1_pin4), .pin2(n7404_1_pin6), .pin3(n7408_2_pin3), .pin4(n7408_2_pin3), .pin5(n7404_1_pin8),
    .pin6(n7408_1_pin12), .pin13(SQC[8]), .pin12(n7408_2_pin12), .pin11(A), .pin10(INSTR[3]), .pin9(SQC[8]),
    .pin8(D));
  ThreeToEight threetoeight_1 (
    .FIn(n7408_1_pin8), .O_111(threetoeight_1_o_111), .O_110(threetoeight_1_o_110),
    .O_101(threetoeight_1_o_101), .O_100(threetoeight_1_o_100), .O_011(threetoeight_1_o_011),
    .O_010(n7432_1_pin9), .O_001(n7432_1_pin13), .O_000(threetoeight_1_o_000));
  Pull_Resistor pull_resistor_1 (.node(pull_resistor_1_node));
  Pull_Resistor pull_resistor_2 (.node(pull_resistor_2_node));
  Pull_Resistor pull_resistor_3 (.node(pull_resistor_3_node));
  _7432 #(.ShowInternalStructure("true")) u_7432_2 (
    .pin1(threetoeight_1_o_110), .pin2(threetoeight_1_o_101), .pin3(n7432_2_pin3),
    .pin4(threetoeight_1_o_100), .pin5(threetoeight_1_o_011), .pin6(n7432_2_pin6), .pin13(n7432_2_pin3),
    .pin12(n7432_2_pin6), .pin11(n7432_2_pin11), .pin10(n7432_2_pin11), .pin9(threetoeight_1_o_111),
    .pin8(n7432_1_pin10));
  _7404 #(.ShowInternalStructure("true")) u_7404_2 (
    .pin1(n7432_1_pin9), .pin2(n7404_2_pin2), .pin3(n7432_1_pin13), .pin4(n7404_2_pin4), .pin5(INSTR[3]),
    .pin6(n7408_2_pin12), .pin13(threetoeight_1_o_111), .pin12(n7404_2_pin12), .pin11(n7432_1_pin11),
    .pin10(n7404_2_pin10), .pin9(n7432_2_pin11), .pin8(n7404_2_pin8));
  ALU2 alu2_1 (
    .CIn(CIn), .BIn({BIn[0], BIn[1], BIn[2], BIn[3], BIn[4], BIn[5], BIn[6], BIn[7]}),
    .UND(pull_resistor_3_node), .ODER(pull_resistor_3_node), .XODER(threetoeight_1_o_000),
    .NICHT(pull_resistor_3_node), .SumOut(alu2_1_sumout));
  ALU1 alu1_1 (
    .BIn({BIn[0], BIn[1], BIn[2], BIn[3], BIn[4], BIn[5], BIn[6], BIn[7]}), .CarryIn(n7432_1_pin9),
    .CIn(pull_resistor_1_node), .SumOut(alu1_1_sumout));  // open: CarryOut
  ALU1 alu1_2 (
    .BIn({BIn[0], BIn[1], BIn[2], BIn[3], BIn[4], BIn[5], BIn[6], BIn[7]}), .CarryIn(pull_resistor_2_node),
    .CIn(CIn), .CarryOut(Cry), .SumOut(alu1_2_sumout));
  ALU2 alu2_2 (
    .CIn(CIn), .BIn({BIn[0], BIn[1], BIn[2], BIn[3], BIn[4], BIn[5], BIn[6], BIn[7]}),
    .UND(threetoeight_1_o_011), .ODER(threetoeight_1_o_100), .XODER(threetoeight_1_o_101),
    .NICHT(threetoeight_1_o_110), .SumOut(alu2_2_sumout));
  _7404 #(.ShowInternalStructure("true")) u_7404_3 (
    .pin5(n7404_3_pin5), .pin6(Zero));  // open: pin1, pin2, pin3, pin4, pin13, pin12, pin11, pin10, pin9, pin8
  _74245 #(.ShowInternalStructure("true")) u_74245_1 (
    .pin1(n74245_1_pin1), .pin2(BIn[0]), .pin3(BIn[7]), .pin4(BIn[6]), .pin5(BIn[5]), .pin6(BIn[4]),
    .pin7(BIn[3]), .pin8(BIn[2]), .pin9(BIn[1]), .pin19(n7404_2_pin12), .pin18(Sign),
    .pin17(n74245_1_pin17[1]), .pin16(n74245_1_pin17[2]), .pin15(n74245_1_pin17[3]),
    .pin14(n74245_1_pin17[4]), .pin13(n74245_1_pin17[5]), .pin12(n74245_1_pin17[6]), .pin11(n74245_1_pin17[7]));
  _74245 #(.ShowInternalStructure("true")) u_74245_2 (
    .pin1(n74245_1_pin1), .pin2(alu1_1_sumout[7]), .pin3(alu1_1_sumout[6]), .pin4(alu1_1_sumout[5]),
    .pin5(alu1_1_sumout[4]), .pin6(alu1_1_sumout[3]), .pin7(alu1_1_sumout[2]), .pin8(alu1_1_sumout[1]),
    .pin9(alu1_1_sumout[0]), .pin19(n7404_2_pin2), .pin18(Sign), .pin17(n74245_1_pin17[1]),
    .pin16(n74245_1_pin17[2]), .pin15(n74245_1_pin17[3]), .pin14(n74245_1_pin17[4]),
    .pin13(n74245_1_pin17[5]), .pin12(n74245_1_pin17[6]), .pin11(n74245_1_pin17[7]));
  _74245 #(.ShowInternalStructure("true")) u_74245_3 (
    .pin1(n74245_1_pin1), .pin2(alu1_2_sumout[7]), .pin3(alu1_2_sumout[6]), .pin4(alu1_2_sumout[5]),
    .pin5(alu1_2_sumout[4]), .pin6(alu1_2_sumout[3]), .pin7(alu1_2_sumout[2]), .pin8(alu1_2_sumout[1]),
    .pin9(alu1_2_sumout[0]), .pin19(n7404_2_pin4), .pin18(Sign), .pin17(n74245_1_pin17[1]),
    .pin16(n74245_1_pin17[2]), .pin15(n74245_1_pin17[3]), .pin14(n74245_1_pin17[4]),
    .pin13(n74245_1_pin17[5]), .pin12(n74245_1_pin17[6]), .pin11(n74245_1_pin17[7]));
  _74245 #(.ShowInternalStructure("true")) u_74245_4 (
    .pin1(n74245_1_pin1), .pin2(alu2_2_sumout[0]), .pin3(alu2_2_sumout[1]), .pin4(alu2_2_sumout[2]),
    .pin5(alu2_2_sumout[3]), .pin6(alu2_2_sumout[4]), .pin7(alu2_2_sumout[5]), .pin8(alu2_2_sumout[6]),
    .pin9(alu2_2_sumout[7]), .pin19(n7404_2_pin8), .pin18(Sign), .pin17(n74245_1_pin17[1]),
    .pin16(n74245_1_pin17[2]), .pin15(n74245_1_pin17[3]), .pin14(n74245_1_pin17[4]),
    .pin13(n74245_1_pin17[5]), .pin12(n74245_1_pin17[6]), .pin11(n74245_1_pin17[7]));
  _74245 #(.ShowInternalStructure("true")) u_74245_5 (
    .pin1(n74245_1_pin1), .pin2(alu2_1_sumout[0]), .pin3(alu2_1_sumout[1]), .pin4(alu2_1_sumout[2]),
    .pin5(alu2_1_sumout[3]), .pin6(alu2_1_sumout[4]), .pin7(alu2_1_sumout[5]), .pin8(alu2_1_sumout[6]),
    .pin9(alu2_1_sumout[7]), .pin19(n7404_1_pin2), .pin18(Sign), .pin17(n74245_1_pin17[1]),
    .pin16(n74245_1_pin17[2]), .pin15(n74245_1_pin17[3]), .pin14(n74245_1_pin17[4]),
    .pin13(n74245_1_pin17[5]), .pin12(n74245_1_pin17[6]), .pin11(n74245_1_pin17[7]));
  Pull_Resistor pull_resistor_4 (.node({n74245_1_pin17, Sign}));
  _74245 #(.ShowInternalStructure("true")) u_74245_6 (
    .pin1(n74245_6_pin1), .pin2(Sign), .pin3(n74245_1_pin17[1]), .pin4(n74245_1_pin17[2]),
    .pin5(n74245_1_pin17[3]), .pin6(n74245_1_pin17[4]), .pin7(n74245_1_pin17[5]), .pin8(n74245_1_pin17[6]),
    .pin9(n74245_1_pin17[7]), .pin19(n7404_2_pin10), .pin18(DOut[0]), .pin17(DOut[1]), .pin16(DOut[2]),
    .pin15(DOut[3]), .pin14(DOut[4]), .pin13(DOut[5]), .pin12(DOut[6]), .pin11(DOut[7]));
  _7432 #(.ShowInternalStructure("true")) u_7432_3 (
    .pin1(Sign), .pin2(n74245_1_pin17[1]), .pin3(n7432_3_pin3), .pin4(n7432_3_pin3),
    .pin5(n74245_1_pin17[2]), .pin6(n7432_3_pin6), .pin13(n74245_1_pin17[4]), .pin12(n7432_3_pin12),
    .pin11(n7432_3_pin11), .pin10(n74245_1_pin17[3]), .pin9(n7432_3_pin6), .pin8(n7432_3_pin12));
  _7432 #(.ShowInternalStructure("true")) u_7432_4 (
    .pin1(n74245_1_pin17[5]), .pin2(n7432_3_pin11), .pin3(n7432_4_pin3), .pin4(n7432_4_pin3),
    .pin5(n74245_1_pin17[6]), .pin6(n7432_4_pin6), .pin13(n74245_1_pin17[7]), .pin12(n7432_4_pin12),
    .pin11(n7404_3_pin5), .pin9(n7432_4_pin6), .pin8(n7432_4_pin12));  // open: pin10
  // also tied to VCC on the sheet: {n74245_1_pin1, n74245_6_pin1}

  // Notes on the sheet:
  //   SQC: initial=0x1
endmodule

module ThreeToEight (
  input  [2:0] FIn,
  output O_111,
  output O_110,
  output O_101,
  output O_100,
  output O_011,
  output O_010,
  output O_001,
  output O_000
);

  wire n7404_1_pin6, n7404_1_pin8, n7404_1_pin10, n7404_1_pin12, n7404_2_pin4, n7404_2_pin6, n7404_2_pin8,
       n7404_2_pin10, n7404_2_pin12, n7411_1_pin5, n7411_1_pin10, n7411_2_pin9;

  _7411 #(.ShowInternalStructure("true")) u_7411_1 (
    .pin1(FIn[1]), .pin2(FIn[2]), .pin3(FIn[2]), .pin4(FIn[1]), .pin5(n7411_1_pin5), .pin6(O_110),
    .pin13(FIn[0]), .pin12(O_111), .pin11(FIn[0]), .pin10(n7411_1_pin10), .pin9(FIn[2]), .pin8(O_101));
  _7404 #(.ShowInternalStructure("true")) u_7404_1 (
    .pin1(FIn[0]), .pin2(n7411_1_pin5), .pin3(FIn[1]), .pin4(n7411_1_pin10), .pin5(FIn[1]),
    .pin6(n7404_1_pin6), .pin13(FIn[2]), .pin12(n7404_1_pin12), .pin11(FIn[2]), .pin10(n7404_1_pin10),
    .pin9(FIn[0]), .pin8(n7404_1_pin8));
  _7411 #(.ShowInternalStructure("true")) u_7411_2 (
    .pin1(n7404_1_pin6), .pin2(FIn[2]), .pin3(n7404_1_pin10), .pin4(FIn[1]), .pin5(FIn[0]), .pin6(O_011),
    .pin13(n7404_1_pin8), .pin12(O_100), .pin11(n7404_1_pin12), .pin10(FIn[1]), .pin9(n7411_2_pin9),
    .pin8(O_010));
  _7404 #(.ShowInternalStructure("true")) u_7404_2 (
    .pin1(FIn[0]), .pin2(n7411_2_pin9), .pin3(FIn[2]), .pin4(n7404_2_pin4), .pin5(FIn[1]),
    .pin6(n7404_2_pin6), .pin13(FIn[2]), .pin12(n7404_2_pin12), .pin11(FIn[1]), .pin10(n7404_2_pin10),
    .pin9(FIn[0]), .pin8(n7404_2_pin8));
  _7411 #(.ShowInternalStructure("true")) u_7411_3 (
    .pin1(n7404_2_pin6), .pin2(n7404_2_pin4), .pin13(FIn[0]), .pin12(O_001), .pin11(n7404_2_pin8),
    .pin10(n7404_2_pin10), .pin9(n7404_2_pin12), .pin8(O_000));  // open: pin3, pin4, pin5, pin6
endmodule

module Fetch (
  input  [23:0] SQC,
  output PCSEL,
  output MER,
  output LINC,
  output LINSTR,
  output INCSEL,
  output PCLOAD
);

  wire n7432_1_pin3, n7432_1_pin11;

  _7432 #(.ShowInternalStructure("true")) u_7432_1 (
    .pin1(SQC[0]), .pin2(SQC[1]), .pin3(n7432_1_pin3), .pin4(n7432_1_pin3), .pin5(SQC[2]), .pin6(MER),
    .pin13(SQC[0]), .pin12(SQC[1]), .pin11(n7432_1_pin11), .pin10(n7432_1_pin11), .pin9(SQC[2]), .pin8(PCSEL));
  _7432 #(.ShowInternalStructure("true")) u_7432_2 (
    .pin1(SQC[3]), .pin2(SQC[4]), .pin3(INCSEL), .pin13(SQC[1]), .pin12(SQC[1]), .pin11(LINSTR));  // open: pin4, pin5, pin6, pin10, pin9, pin8

  assign LINC = SQC[1];
  assign PCLOAD = SQC[3];
endmodule

module Dual_Register (
  input  [7:0] DIn,
  input  CLK,
  input  LOAD1,
  input  LOAD2,
  input  SELECT1,
  input  SELECT2,
  input  LOAD12,
  input  SELECT12,
  input  [15:0] D16In,
  output [7:0] DOut,
  output [15:0] D16Out
);

  wire n7404_1_pin2, n7404_1_pin4, n7404_1_pin6, n7404_1_pin8, n7404_1_pin12, n7432_1_pin1, n7432_1_pin2,
       n7432_1_pin3, n7432_1_pin5, n74245_1_pin1, n74245_1_pin19, n74245_2_pin1, n74245_3_pin1,
       n74245_4_pin1, n74245_5_pin1, n74245_6_pin1, n74245_7_pin1, n74245_8_pin1, n74273_1_pin11;
  wire [7:0] n74245_1_pin11, n74245_3_pin18, n74273_1_pin2, n74273_2_pin2;

  _74245 #(.ShowInternalStructure("true")) u_74245_1 (
    .pin1(n74245_1_pin1), .pin2(DIn[0]), .pin3(DIn[1]), .pin4(DIn[2]), .pin5(DIn[3]), .pin6(DIn[4]),
    .pin7(DIn[5]), .pin8(DIn[6]), .pin9(DIn[7]), .pin19(n74245_1_pin19), .pin18(n74245_1_pin11[7]),
    .pin17(n74245_1_pin11[6]), .pin16(n74245_1_pin11[5]), .pin15(n74245_1_pin11[4]),
    .pin14(n74245_1_pin11[3]), .pin13(n74245_1_pin11[2]), .pin12(n74245_1_pin11[1]), .pin11(n74245_1_pin11[0]));
  Pull_Resistor pull_resistor_1 (.node(n74245_1_pin11));
  _7404 #(.ShowInternalStructure("true")) u_7404_1 (
    .pin1(SELECT2), .pin2(n7404_1_pin2), .pin3(SELECT12), .pin4(n7404_1_pin4), .pin5(LOAD12),
    .pin6(n7404_1_pin6), .pin13(SELECT1), .pin12(n7404_1_pin12), .pin11(LOAD1), .pin10(n74245_1_pin19),
    .pin9(LOAD2), .pin8(n7404_1_pin8));
  _74245 #(.ShowInternalStructure("true")) u_74245_2 (
    .pin1(n74245_2_pin1), .pin2(D16In[7]), .pin3(D16In[6]), .pin4(D16In[5]), .pin5(D16In[4]),
    .pin6(D16In[3]), .pin7(D16In[2]), .pin8(D16In[1]), .pin9(D16In[0]), .pin19(n7404_1_pin6),
    .pin18(n74245_1_pin11[0]), .pin17(n74245_1_pin11[1]), .pin16(n74245_1_pin11[2]),
    .pin15(n74245_1_pin11[3]), .pin14(n74245_1_pin11[4]), .pin13(n74245_1_pin11[5]),
    .pin12(n74245_1_pin11[6]), .pin11(n74245_1_pin11[7]));
  _74245 #(.ShowInternalStructure("true")) u_74245_3 (
    .pin1(n74245_3_pin1), .pin2(D16In[8]), .pin3(D16In[9]), .pin4(D16In[10]), .pin5(D16In[11]),
    .pin6(D16In[12]), .pin7(D16In[13]), .pin8(D16In[14]), .pin9(D16In[15]), .pin19(n7404_1_pin6),
    .pin18(n74245_3_pin18[0]), .pin17(n74245_3_pin18[1]), .pin16(n74245_3_pin18[2]),
    .pin15(n74245_3_pin18[3]), .pin14(n74245_3_pin18[4]), .pin13(n74245_3_pin18[5]),
    .pin12(n74245_3_pin18[6]), .pin11(n74245_3_pin18[7]));
  _74273 #(.ShowInternalStructure("true")) u_74273_1 (
    .pin2(n74273_1_pin2[0]), .pin3(n74245_1_pin11[0]), .pin4(n74245_1_pin11[1]), .pin5(n74273_1_pin2[1]),
    .pin6(n74273_1_pin2[2]), .pin7(n74245_1_pin11[2]), .pin8(n74245_1_pin11[3]), .pin9(n74273_1_pin2[3]),
    .pin19(n74273_1_pin2[7]), .pin18(n74245_1_pin11[7]), .pin17(n74245_1_pin11[6]), .pin16(n74273_1_pin2[6]),
    .pin15(n74273_1_pin2[5]), .pin14(n74245_1_pin11[5]), .pin13(n74245_1_pin11[4]), .pin12(n74273_1_pin2[4]),
    .pin11(n74273_1_pin11));  // open: pin1
  _7432 #(.ShowInternalStructure("true")) u_7432_1 (
    .pin1(n7432_1_pin1), .pin2(n7432_1_pin2), .pin3(n7432_1_pin3), .pin4(n7432_1_pin2), .pin5(n7432_1_pin5),
    .pin6(n74273_1_pin11));  // open: pin13, pin12, pin11, pin10, pin9, pin8
  _7408 #(.ShowInternalStructure("true")) u_7408_1 (
    .pin1(LOAD1), .pin2(CLK), .pin3(n7432_1_pin5), .pin4(CLK), .pin5(LOAD2), .pin6(n7432_1_pin1),
    .pin13(LOAD12), .pin12(CLK), .pin11(n7432_1_pin2));  // open: pin10, pin9, pin8
  _74245 #(.ShowInternalStructure("true")) u_74245_4 (
    .pin1(n74245_4_pin1), .pin2(DIn[0]), .pin3(DIn[1]), .pin4(DIn[2]), .pin5(DIn[3]), .pin6(DIn[4]),
    .pin7(DIn[5]), .pin8(DIn[6]), .pin9(DIn[7]), .pin19(n7404_1_pin8), .pin18(n74245_3_pin18[0]),
    .pin17(n74245_3_pin18[1]), .pin16(n74245_3_pin18[2]), .pin15(n74245_3_pin18[3]),
    .pin14(n74245_3_pin18[4]), .pin13(n74245_3_pin18[5]), .pin12(n74245_3_pin18[6]), .pin11(n74245_3_pin18[7]));
  Pull_Resistor pull_resistor_2 (.node(n74245_3_pin18));
  _74273 #(.ShowInternalStructure("true")) u_74273_2 (
    .pin2(n74273_2_pin2[0]), .pin3(n74245_3_pin18[0]), .pin4(n74245_3_pin18[1]), .pin5(n74273_2_pin2[1]),
    .pin6(n74273_2_pin2[2]), .pin7(n74245_3_pin18[2]), .pin8(n74245_3_pin18[3]), .pin9(n74273_2_pin2[3]),
    .pin19(n74273_2_pin2[7]), .pin18(n74245_3_pin18[7]), .pin17(n74245_3_pin18[6]), .pin16(n74273_2_pin2[6]),
    .pin15(n74273_2_pin2[5]), .pin14(n74245_3_pin18[5]), .pin13(n74245_3_pin18[4]), .pin12(n74273_2_pin2[4]),
    .pin11(n7432_1_pin3));  // open: pin1
  _74245 #(.ShowInternalStructure("true")) u_74245_5 (
    .pin1(n74245_5_pin1), .pin2(n74273_1_pin2[7]), .pin3(n74273_1_pin2[6]), .pin4(n74273_1_pin2[5]),
    .pin5(n74273_1_pin2[4]), .pin6(n74273_1_pin2[3]), .pin7(n74273_1_pin2[2]), .pin8(n74273_1_pin2[1]),
    .pin9(n74273_1_pin2[0]), .pin19(n7404_1_pin12), .pin18(DOut[7]), .pin17(DOut[6]), .pin16(DOut[5]),
    .pin15(DOut[4]), .pin14(DOut[3]), .pin13(DOut[2]), .pin12(DOut[1]), .pin11(DOut[0]));
  _74245 #(.ShowInternalStructure("true")) u_74245_6 (
    .pin1(n74245_6_pin1), .pin2(n74273_2_pin2[7]), .pin3(n74273_2_pin2[6]), .pin4(n74273_2_pin2[5]),
    .pin5(n74273_2_pin2[4]), .pin6(n74273_2_pin2[3]), .pin7(n74273_2_pin2[2]), .pin8(n74273_2_pin2[1]),
    .pin9(n74273_2_pin2[0]), .pin19(n7404_1_pin2), .pin18(DOut[7]), .pin17(DOut[6]), .pin16(DOut[5]),
    .pin15(DOut[4]), .pin14(DOut[3]), .pin13(DOut[2]), .pin12(DOut[1]), .pin11(DOut[0]));
  _74245 #(.ShowInternalStructure("true")) u_74245_7 (
    .pin1(n74245_7_pin1), .pin2(n74273_1_pin2[0]), .pin3(n74273_1_pin2[1]), .pin4(n74273_1_pin2[2]),
    .pin5(n74273_1_pin2[3]), .pin6(n74273_1_pin2[4]), .pin7(n74273_1_pin2[5]), .pin8(n74273_1_pin2[6]),
    .pin9(n74273_1_pin2[7]), .pin19(n7404_1_pin4), .pin18(D16Out[7]), .pin17(D16Out[6]), .pin16(D16Out[5]),
    .pin15(D16Out[4]), .pin14(D16Out[3]), .pin13(D16Out[2]), .pin12(D16Out[1]), .pin11(D16Out[0]));
  _74245 #(.ShowInternalStructure("true")) u_74245_8 (
    .pin1(n74245_8_pin1), .pin2(n74273_2_pin2[0]), .pin3(n74273_2_pin2[1]), .pin4(n74273_2_pin2[2]),
    .pin5(n74273_2_pin2[3]), .pin6(n74273_2_pin2[4]), .pin7(n74273_2_pin2[5]), .pin8(n74273_2_pin2[6]),
    .pin9(n74273_2_pin2[7]), .pin19(n7404_1_pin4), .pin18(D16Out[8]), .pin17(D16Out[9]), .pin16(D16Out[10]),
    .pin15(D16Out[11]), .pin14(D16Out[12]), .pin13(D16Out[13]), .pin12(D16Out[14]), .pin11(D16Out[15]));
  // also tied to VCC on the sheet: {n74245_1_pin1, n74245_2_pin1, n74245_3_pin1, n74245_4_pin1, n74245_5_pin1, n74245_6_pin1, n74245_7_pin1, n74245_8_pin1}
endmodule

module Dual_Regist_B_C (
  input  [7:0] DIn,
  input  CLK,
  input  LOAD1,
  input  LOAD2,
  input  SELECT1,
  input  SELECT2,
  input  LOAD12,
  input  SELECT12,
  input  [15:0] D16In,
  output [7:0] BOut,
  output [7:0] COut,
  output [15:0] D16Out
);

  wire n7404_1_pin4, n7404_1_pin6, n7404_1_pin8, n7432_1_pin1, n7432_1_pin2, n7432_1_pin3, n7432_1_pin5,
       n74245_1_pin1, n74245_1_pin19, n74245_2_pin1, n74245_3_pin1, n74245_4_pin1, n74245_5_pin1,
       n74245_6_pin1, n74273_1_pin11;
  wire [7:0] n74245_1_pin18, n74245_3_pin18;

  _74245 #(.ShowInternalStructure("true")) u_74245_1 (
    .pin1(n74245_1_pin1), .pin2(DIn[0]), .pin3(DIn[1]), .pin4(DIn[2]), .pin5(DIn[3]), .pin6(DIn[4]),
    .pin7(DIn[5]), .pin8(DIn[6]), .pin9(DIn[7]), .pin19(n74245_1_pin19), .pin18(n74245_1_pin18[0]),
    .pin17(n74245_1_pin18[1]), .pin16(n74245_1_pin18[2]), .pin15(n74245_1_pin18[3]),
    .pin14(n74245_1_pin18[4]), .pin13(n74245_1_pin18[5]), .pin12(n74245_1_pin18[6]), .pin11(n74245_1_pin18[7]));
  Pull_Resistor pull_resistor_1 (.node(n74245_1_pin18));
  _7404 #(.ShowInternalStructure("true")) u_7404_1 (
    .pin1(SELECT2), .pin3(SELECT12), .pin4(n7404_1_pin4), .pin5(LOAD12), .pin6(n7404_1_pin6),
    .pin13(SELECT1), .pin11(LOAD1), .pin10(n74245_1_pin19), .pin9(LOAD2), .pin8(n7404_1_pin8));  // open: pin2, pin12
  _74245 #(.ShowInternalStructure("true")) u_74245_2 (
    .pin1(n74245_2_pin1), .pin2(D16In[7]), .pin3(D16In[6]), .pin4(D16In[5]), .pin5(D16In[4]),
    .pin6(D16In[3]), .pin7(D16In[2]), .pin8(D16In[1]), .pin9(D16In[0]), .pin19(n7404_1_pin6),
    .pin18(n74245_1_pin18[0]), .pin17(n74245_1_pin18[1]), .pin16(n74245_1_pin18[2]),
    .pin15(n74245_1_pin18[3]), .pin14(n74245_1_pin18[4]), .pin13(n74245_1_pin18[5]),
    .pin12(n74245_1_pin18[6]), .pin11(n74245_1_pin18[7]));
  _74245 #(.ShowInternalStructure("true")) u_74245_3 (
    .pin1(n74245_3_pin1), .pin2(D16In[8]), .pin3(D16In[9]), .pin4(D16In[10]), .pin5(D16In[11]),
    .pin6(D16In[12]), .pin7(D16In[13]), .pin8(D16In[14]), .pin9(D16In[15]), .pin19(n7404_1_pin6),
    .pin18(n74245_3_pin18[0]), .pin17(n74245_3_pin18[1]), .pin16(n74245_3_pin18[2]),
    .pin15(n74245_3_pin18[3]), .pin14(n74245_3_pin18[4]), .pin13(n74245_3_pin18[5]),
    .pin12(n74245_3_pin18[6]), .pin11(n74245_3_pin18[7]));
  _74273 #(.ShowInternalStructure("true")) u_74273_1 (
    .pin2(BOut[0]), .pin3(n74245_1_pin18[0]), .pin4(n74245_1_pin18[1]), .pin5(BOut[1]), .pin6(BOut[2]),
    .pin7(n74245_1_pin18[2]), .pin8(n74245_1_pin18[3]), .pin9(BOut[3]), .pin19(BOut[7]),
    .pin18(n74245_1_pin18[7]), .pin17(n74245_1_pin18[6]), .pin16(BOut[6]), .pin15(BOut[5]),
    .pin14(n74245_1_pin18[5]), .pin13(n74245_1_pin18[4]), .pin12(BOut[4]), .pin11(n74273_1_pin11));  // open: pin1
  _7432 #(.ShowInternalStructure("true")) u_7432_1 (
    .pin1(n7432_1_pin1), .pin2(n7432_1_pin2), .pin3(n7432_1_pin3), .pin4(n7432_1_pin2), .pin5(n7432_1_pin5),
    .pin6(n74273_1_pin11));  // open: pin13, pin12, pin11, pin10, pin9, pin8
  _7408 #(.ShowInternalStructure("true")) u_7408_1 (
    .pin1(LOAD1), .pin2(CLK), .pin3(n7432_1_pin5), .pin4(CLK), .pin5(LOAD2), .pin6(n7432_1_pin1),
    .pin13(LOAD12), .pin12(CLK), .pin11(n7432_1_pin2));  // open: pin10, pin9, pin8
  _74245 #(.ShowInternalStructure("true")) u_74245_4 (
    .pin1(n74245_4_pin1), .pin2(DIn[0]), .pin3(DIn[1]), .pin4(DIn[2]), .pin5(DIn[3]), .pin6(DIn[4]),
    .pin7(DIn[5]), .pin8(DIn[6]), .pin9(DIn[7]), .pin19(n7404_1_pin8), .pin18(n74245_3_pin18[0]),
    .pin17(n74245_3_pin18[1]), .pin16(n74245_3_pin18[2]), .pin15(n74245_3_pin18[3]),
    .pin14(n74245_3_pin18[4]), .pin13(n74245_3_pin18[5]), .pin12(n74245_3_pin18[6]), .pin11(n74245_3_pin18[7]));
  Pull_Resistor pull_resistor_2 (.node(n74245_3_pin18));
  _74273 #(.ShowInternalStructure("true")) u_74273_2 (
    .pin2(COut[0]), .pin3(n74245_3_pin18[0]), .pin4(n74245_3_pin18[1]), .pin5(COut[1]), .pin6(COut[2]),
    .pin7(n74245_3_pin18[2]), .pin8(n74245_3_pin18[3]), .pin9(COut[3]), .pin19(COut[7]),
    .pin18(n74245_3_pin18[7]), .pin17(n74245_3_pin18[6]), .pin16(COut[6]), .pin15(COut[5]),
    .pin14(n74245_3_pin18[5]), .pin13(n74245_3_pin18[4]), .pin12(COut[4]), .pin11(n7432_1_pin3));  // open: pin1
  _74245 #(.ShowInternalStructure("true")) u_74245_5 (
    .pin1(n74245_5_pin1), .pin2(BOut[7]), .pin3(BOut[6]), .pin4(BOut[5]), .pin5(BOut[4]), .pin6(BOut[3]),
    .pin7(BOut[2]), .pin8(BOut[1]), .pin9(BOut[0]), .pin19(n7404_1_pin4), .pin18(D16Out[0]),
    .pin17(D16Out[1]), .pin16(D16Out[2]), .pin15(D16Out[3]), .pin14(D16Out[4]), .pin13(D16Out[5]),
    .pin12(D16Out[6]), .pin11(D16Out[7]));
  _74245 #(.ShowInternalStructure("true")) u_74245_6 (
    .pin1(n74245_6_pin1), .pin2(COut[0]), .pin3(COut[1]), .pin4(COut[2]), .pin5(COut[3]), .pin6(COut[4]),
    .pin7(COut[5]), .pin8(COut[6]), .pin9(COut[7]), .pin19(n7404_1_pin4), .pin18(D16Out[8]),
    .pin17(D16Out[9]), .pin16(D16Out[10]), .pin15(D16Out[11]), .pin14(D16Out[12]), .pin13(D16Out[13]),
    .pin12(D16Out[14]), .pin11(D16Out[15]));
  // also tied to VCC on the sheet: {n74245_1_pin1, n74245_2_pin1, n74245_3_pin1, n74245_4_pin1, n74245_5_pin1, n74245_6_pin1}
endmodule

module Incrementer (
  input  CLK,
  input  LoadINC,
  input  [15:0] AIn,
  input  SELECTINC,
  output [15:0] AOut
);

  wire alu1_1_carryout, n7404_1_pin2, n74245_1_pin1, n74245_2_pin1;
  wire [7:0] alu1_1_sumout, alu1_2_sumout, dual_regist_b_c_1_bout, dual_regist_b_c_1_cout,
       pull_resistor_1_node, pull_resistor_2_node;

  _7404 #(.ShowInternalStructure("true")) u_7404_1 (
    .pin1(SELECTINC), .pin2(n7404_1_pin2));  // open: pin3, pin4, pin5, pin6, pin13, pin12, pin11, pin10, pin9, pin8
  Dual_Regist_B_C dual_regist_b_c_1 (
    .CLK(CLK), .LOAD12(LoadINC), .D16In(AIn), .BOut(dual_regist_b_c_1_bout),
    .COut({dual_regist_b_c_1_cout[0], dual_regist_b_c_1_cout[1], dual_regist_b_c_1_cout[2], dual_regist_b_c_1_cout[3], dual_regist_b_c_1_cout[4], dual_regist_b_c_1_cout[5], dual_regist_b_c_1_cout[6], dual_regist_b_c_1_cout[7]}));  // open: DIn, LOAD1, LOAD2, SELECT1, SELECT2, SELECT12, D16Out
  Pull_Resistor pull_resistor_1 (.node(pull_resistor_1_node));
  Pull_Resistor pull_resistor_2 (.node(pull_resistor_2_node));
  ALU1 alu1_1 (
    .BIn(dual_regist_b_c_1_bout), .CarryIn(1'b1), .CIn(pull_resistor_1_node), .CarryOut(alu1_1_carryout),
    .SumOut(alu1_1_sumout));
  ALU1 alu1_2 (
    .BIn(dual_regist_b_c_1_cout), .CarryIn(alu1_1_carryout), .CIn(pull_resistor_2_node),
    .SumOut(alu1_2_sumout));  // open: CarryOut
  _74245 #(.ShowInternalStructure("true")) u_74245_1 (
    .pin1(n74245_1_pin1), .pin2(alu1_1_sumout[0]), .pin3(alu1_1_sumout[1]), .pin4(alu1_1_sumout[2]),
    .pin5(alu1_1_sumout[3]), .pin6(alu1_1_sumout[4]), .pin7(alu1_1_sumout[5]), .pin8(alu1_1_sumout[6]),
    .pin9(alu1_1_sumout[7]), .pin19(n7404_1_pin2), .pin18(AOut[0]), .pin17(AOut[1]), .pin16(AOut[2]),
    .pin15(AOut[3]), .pin14(AOut[4]), .pin13(AOut[5]), .pin12(AOut[6]), .pin11(AOut[7]));
  _74245 #(.ShowInternalStructure("true")) u_74245_2 (
    .pin1(n74245_2_pin1), .pin2(alu1_2_sumout[0]), .pin3(alu1_2_sumout[1]), .pin4(alu1_2_sumout[2]),
    .pin5(alu1_2_sumout[3]), .pin6(alu1_2_sumout[4]), .pin7(alu1_2_sumout[5]), .pin8(alu1_2_sumout[6]),
    .pin9(alu1_2_sumout[7]), .pin19(n7404_1_pin2), .pin18(AOut[8]), .pin17(AOut[9]), .pin16(AOut[10]),
    .pin15(AOut[11]), .pin14(AOut[12]), .pin13(AOut[13]), .pin12(AOut[14]), .pin11(AOut[15]));
  // also tied to VCC on the sheet: {n74245_1_pin1, n74245_2_pin1}
endmodule

module Instr_Decoder (
  input  [7:0] in_1,
  output setab,
  output mov8,
  output goto,
  output alu,
  output load,
  output store,
  output mov16,
  output OUT_8,
  output HALT,
  output IN_8,
  output inc
);

  wire n7404_1_pin2, n7404_1_pin4, n7404_1_pin6, n7404_1_pin8, n7404_1_pin10, n7404_1_pin12, n7404_2_pin2,
       n7404_2_pin4, n7408_1_pin6, n7408_2_pin3, n7408_2_pin6, n7408_2_pin11, n7408_3_pin3, n7408_3_pin6,
       n7408_3_pin8, n7408_3_pin11, n7408_4_pin3, n7408_4_pin6, n7408_4_pin8, n7408_4_pin11, n7408_5_pin3,
       n7408_5_pin5, n7408_5_pin11, n7408_6_pin1, n7408_6_pin3, n7408_7_pin3, n7408_7_pin6, n7408_7_pin8,
       n7408_7_pin11, n7408_8_pin1, n7408_8_pin3, n7408_8_pin11, n7408_9_pin3, n7408_9_pin11, n7408_10_pin2,
       n7408_10_pin3, n7408_10_pin11, n7408_11_pin1, n7408_11_pin3, n7408_11_pin6, n7408_11_pin11,
       n7408_12_pin2, n7408_12_pin3, n7408_12_pin6, n7408_12_pin11, n7408_14_pin2, n7408_14_pin3,
       n7408_14_pin6, n7408_14_pin11, n7408_15_pin3, n7408_15_pin6;

  _7404 #(.ShowInternalStructure("true")) u_7404_1 (
    .pin1(in_1[7]), .pin2(n7404_1_pin2), .pin3(in_1[6]), .pin4(n7404_1_pin4), .pin5(in_1[5]),
    .pin6(n7404_1_pin6), .pin13(in_1[4]), .pin12(n7404_1_pin12), .pin11(in_1[3]), .pin10(n7404_1_pin10),
    .pin9(in_1[2]), .pin8(n7404_1_pin8));
  _7404 #(.ShowInternalStructure("true")) u_7404_2 (
    .pin1(in_1[0]), .pin2(n7404_2_pin2), .pin3(in_1[1]), .pin4(n7404_2_pin4), .pin11(n7404_2_pin4));  // open: pin5, pin6, pin13, pin12, pin10, pin9, pin8
  _7408 #(.ShowInternalStructure("true")) u_7408_1 (
    .pin1(n7404_1_pin2), .pin2(in_1[6]), .pin3(setab), .pin4(n7404_1_pin4), .pin5(in_1[7]),
    .pin6(n7408_1_pin6), .pin13(n7404_1_pin2), .pin12(n7404_1_pin4), .pin11(mov8), .pin10(in_1[7]),
    .pin9(in_1[6]), .pin8(goto));
  _7408 #(.ShowInternalStructure("true")) u_7408_2 (
    .pin1(in_1[7]), .pin2(n7404_1_pin4), .pin3(n7408_2_pin3), .pin4(n7408_2_pin3), .pin5(n7404_1_pin6),
    .pin6(n7408_2_pin6), .pin13(n7408_1_pin6), .pin12(n7404_1_pin6), .pin11(n7408_2_pin11),
    .pin10(n7408_2_pin11), .pin9(n7404_1_pin12), .pin8(alu));
  _7408 #(.ShowInternalStructure("true")) u_7408_3 (
    .pin1(n7408_2_pin6), .pin2(in_1[4]), .pin3(n7408_3_pin3), .pin4(n7408_3_pin3), .pin5(n7404_1_pin10),
    .pin6(n7408_3_pin6), .pin13(in_1[7]), .pin12(n7404_1_pin4), .pin11(n7408_3_pin11), .pin10(n7408_3_pin11),
    .pin9(n7404_1_pin6), .pin8(n7408_3_pin8));
  _7408 #(.ShowInternalStructure("true")) u_7408_4 (
    .pin1(in_1[7]), .pin2(n7404_1_pin4), .pin3(n7408_4_pin3), .pin4(n7408_4_pin3), .pin5(in_1[5]),
    .pin6(n7408_4_pin6), .pin13(n7408_3_pin8), .pin12(in_1[4]), .pin11(n7408_4_pin11), .pin10(n7408_4_pin11),
    .pin9(in_1[3]), .pin8(n7408_4_pin8));
  _7408 #(.ShowInternalStructure("true")) u_7408_5 (
    .pin1(n7404_1_pin10), .pin2(n7404_1_pin10), .pin3(n7408_5_pin3), .pin4(n7408_5_pin3),
    .pin5(n7408_5_pin5), .pin6(mov16), .pin13(n7404_1_pin10), .pin12(n7408_3_pin6), .pin11(n7408_5_pin11),
    .pin10(n7404_1_pin8), .pin9(n7408_4_pin8), .pin8(store));
  _7408 #(.ShowInternalStructure("true")) u_7408_6 (
    .pin1(n7408_6_pin1), .pin2(n7404_2_pin4), .pin3(n7408_6_pin3), .pin13(n7404_1_pin8),
    .pin12(n7408_5_pin11), .pin11(load));  // open: pin4, pin5, pin6, pin10, pin9, pin8
  _7408 #(.ShowInternalStructure("true")) u_7408_7 (
    .pin1(n7408_4_pin6), .pin2(in_1[4]), .pin3(n7408_7_pin3), .pin4(n7408_7_pin3), .pin5(n7404_1_pin10),
    .pin6(n7408_7_pin6), .pin13(in_1[7]), .pin12(n7404_1_pin4), .pin11(n7408_7_pin11), .pin10(n7408_7_pin11),
    .pin9(in_1[5]), .pin8(n7408_7_pin8));
  _7408 #(.ShowInternalStructure("true")) u_7408_8 (
    .pin1(n7408_8_pin1), .pin2(n7404_2_pin2), .pin3(n7408_8_pin3), .pin4(n7408_8_pin3), .pin5(n7404_2_pin4),
    .pin6(inc), .pin13(n7408_7_pin6), .pin12(n7404_1_pin10), .pin11(n7408_8_pin11), .pin10(n7408_8_pin11),
    .pin9(n7404_1_pin8), .pin8(n7408_8_pin1));
  _7408 #(.ShowInternalStructure("true")) u_7408_9 (
    .pin1(in_1[7]), .pin2(n7404_1_pin4), .pin3(n7408_9_pin3), .pin4(n7408_9_pin3), .pin5(in_1[5]),
    .pin13(n7408_7_pin8), .pin12(n7404_1_pin12), .pin11(n7408_9_pin11), .pin10(n7408_9_pin11),
    .pin9(n7404_1_pin4), .pin8(n7408_5_pin5));  // open: pin6
  _7408 #(.ShowInternalStructure("true")) u_7408_10 (
    .pin1(n7404_1_pin10), .pin2(n7408_10_pin2), .pin3(n7408_10_pin3), .pin4(n7408_10_pin3), .pin5(in_1[2]),
    .pin6(n7408_6_pin1), .pin13(in_1[7]), .pin12(n7404_1_pin4), .pin11(n7408_10_pin11),
    .pin10(n7408_10_pin11), .pin9(n7404_1_pin6), .pin8(n7408_10_pin2));
  _7408 #(.ShowInternalStructure("true")) u_7408_11 (
    .pin1(n7408_11_pin1), .pin2(in_1[2]), .pin3(n7408_11_pin3), .pin4(n7408_11_pin3), .pin5(n7404_2_pin4),
    .pin6(n7408_11_pin6), .pin13(n7408_10_pin2), .pin12(in_1[4]), .pin11(n7408_11_pin11),
    .pin10(n7408_11_pin11), .pin9(in_1[3]), .pin8(n7408_11_pin1));
  _7408 #(.ShowInternalStructure("true")) u_7408_12 (
    .pin1(in_1[4]), .pin2(n7408_12_pin2), .pin3(n7408_12_pin3), .pin4(n7408_12_pin3), .pin5(in_1[2]),
    .pin6(n7408_12_pin6), .pin13(in_1[7]), .pin12(n7404_1_pin4), .pin11(n7408_12_pin11),
    .pin10(n7408_12_pin11), .pin9(n7404_1_pin6), .pin8(n7408_12_pin2));
  _7408 #(.ShowInternalStructure("true")) u_7408_13 (
    .pin1(n7408_12_pin6), .pin2(n7404_1_pin10), .pin3(OUT_8), .pin4(n7408_11_pin6), .pin5(n7404_2_pin2),
    .pin6(HALT));  // open: pin13, pin12, pin11, pin10, pin9, pin8
  _7408 #(.ShowInternalStructure("true")) u_7408_14 (
    .pin1(in_1[4]), .pin2(n7408_14_pin2), .pin3(n7408_14_pin3), .pin4(n7408_14_pin3), .pin5(in_1[3]),
    .pin6(n7408_14_pin6), .pin13(in_1[7]), .pin12(n7404_1_pin4), .pin11(n7408_14_pin11),
    .pin10(n7408_14_pin11), .pin9(n7404_1_pin6), .pin8(n7408_14_pin2));
  _7408 #(.ShowInternalStructure("true")) u_7408_15 (
    .pin1(n7408_14_pin6), .pin2(in_1[2]), .pin3(n7408_15_pin3), .pin4(n7408_15_pin3), .pin5(n7404_2_pin4),
    .pin6(n7408_15_pin6), .pin10(in_1[0]), .pin9(n7408_15_pin6), .pin8(IN_8));  // open: pin13, pin12, pin11
endmodule

module MOV8 (
  input  [23:0] SQC,
  input  [7:0] INSTR,
  output [7:0] LOAD,
  output [7:0] SEL
);

  wire n7404_1_pin2, n7404_1_pin4, n7432_1_pin8, n7432_1_pin11, n74245_1_pin1, n74245_2_pin1;
  wire [7:0] threetoeight_1_o_000, threetoeight_2_o_111;

  _7432 #(.ShowInternalStructure("true")) u_7432_1 (
    .pin13(SQC[7]), .pin12(SQC[6]), .pin11(n7432_1_pin11), .pin10(n7432_1_pin11), .pin9(SQC[5]),
    .pin8(n7432_1_pin8));  // open: pin1, pin2, pin3, pin4, pin5, pin6
  _7404 #(.ShowInternalStructure("true")) u_7404_1 (
    .pin1(SQC[6]), .pin2(n7404_1_pin2), .pin3(n7432_1_pin8), .pin4(n7404_1_pin4));  // open: pin5, pin6, pin13, pin12, pin11, pin10, pin9, pin8
  ThreeToEight threetoeight_1 (
    .FIn({INSTR[3], INSTR[4], INSTR[5]}), .O_111(threetoeight_1_o_000[7]), .O_110(threetoeight_1_o_000[6]),
    .O_101(threetoeight_1_o_000[5]), .O_100(threetoeight_1_o_000[4]), .O_011(threetoeight_1_o_000[3]),
    .O_010(threetoeight_1_o_000[2]), .O_001(threetoeight_1_o_000[1]), .O_000(threetoeight_1_o_000[0]));
  ThreeToEight threetoeight_2 (
    .FIn(INSTR[2:0]), .O_111(threetoeight_2_o_111[0]), .O_110(threetoeight_2_o_111[1]),
    .O_101(threetoeight_2_o_111[2]), .O_100(threetoeight_2_o_111[3]), .O_011(threetoeight_2_o_111[4]),
    .O_010(threetoeight_2_o_111[5]), .O_001(threetoeight_2_o_111[6]), .O_000(threetoeight_2_o_111[7]));
  _74245 #(.ShowInternalStructure("true")) u_74245_1 (
    .pin1(n74245_1_pin1), .pin2(threetoeight_1_o_000[0]), .pin3(threetoeight_1_o_000[1]),
    .pin4(threetoeight_1_o_000[2]), .pin5(threetoeight_1_o_000[3]), .pin6(threetoeight_1_o_000[4]),
    .pin7(threetoeight_1_o_000[5]), .pin8(threetoeight_1_o_000[6]), .pin9(threetoeight_1_o_000[7]),
    .pin19(n7404_1_pin2), .pin18(SEL[0]), .pin17(SEL[1]), .pin16(SEL[2]), .pin15(SEL[3]), .pin14(SEL[4]),
    .pin13(SEL[5]), .pin12(SEL[6]), .pin11(SEL[7]));
  _74245 #(.ShowInternalStructure("true")) u_74245_2 (
    .pin1(n74245_2_pin1), .pin2(threetoeight_2_o_111[7]), .pin3(threetoeight_2_o_111[6]),
    .pin4(threetoeight_2_o_111[5]), .pin5(threetoeight_2_o_111[4]), .pin6(threetoeight_2_o_111[3]),
    .pin7(threetoeight_2_o_111[2]), .pin8(threetoeight_2_o_111[1]), .pin9(threetoeight_2_o_111[0]),
    .pin19(n7404_1_pin4), .pin18(LOAD[7]), .pin17(LOAD[6]), .pin16(LOAD[5]), .pin15(LOAD[4]),
    .pin14(LOAD[3]), .pin13(LOAD[2]), .pin12(LOAD[1]), .pin11(LOAD[0]));
  Pull_Resistor pull_resistor_1 (.node(SEL));
  Pull_Resistor pull_resistor_2 (.node(LOAD));
  // also tied to VCC on the sheet: {n74245_1_pin1, n74245_2_pin1}
endmodule

module INSTRUCTIONS (
  input  MOV_8,
  input  [23:0] SQC,
  input  [7:0] INSTR,
  input  LOAD_8,
  input  [2:0] F,
  input  SAVE_8,
  input  SET_AB,
  input  GOTO_16,
  input  [7:0] REG_IN,
  input  [15:0] Sequence_Extra,
  output [7:0] REG_SELECT,
  output [7:0] REG_LOAD,
  output M_SEL,
  output PC_SEL,
  output MEW,
  output MER,
  output ALOAD,
  output BLOAD,
  output [7:0] DOut,
  output J1_LOAD,
  output M1_LOAD,
  output J2_LOAD,
  output M2_LOAD,
  output INC_LOAD,
  output J_SEL,
  output PC_LOAD,
  output INC_SEL,
  output AT_08
);

  wire goto_1_jsel, goto_1_mer, goto_1_msel, goto_1_pcsel, load_1_mer, load_1_msel, load_1_pcsel,
       n7432_1_pin3, n7432_1_pin11, save_1_msel, save_1_pcsel, undriven;
  wire [7:0] gate_8_1_dout, gate_8_2_dout, gate_8_3_dout, gate_8_4_dout, gate_8_5_dout, gate_8_6_dout,
       gate_8_7_dout, gate_8_8_dout, gate_8_9_dout, gate_8_10_dout, load_1_reg_load, mov8_1_load, mov8_1_sel,
       or_8_2_out_1, save_1_reg_select;
  wire [23:0] gate_24_1_dout, gate_24_2_dout, gate_24_3_dout, gate_24_4_dout, gate_24_5_dout, gate_24_6_dout;

  GATE_24 gate_24_1 (.EN(MOV_8), .DIn(SQC), .DOut(gate_24_1_dout));
  GATE_24 gate_24_2 (.EN(LOAD_8), .DIn(SQC), .DOut(gate_24_2_dout));
  GATE_24 gate_24_3 (.EN(SAVE_8), .DIn(SQC), .DOut(gate_24_3_dout));
  GATE_24 gate_24_4 (.EN(SET_AB), .DIn(SQC), .DOut(gate_24_4_dout));
  GATE_24 gate_24_5 (.EN(GOTO_16), .DIn(SQC), .DOut(gate_24_5_dout));
  GATE_8 gate_8_1 (.EN(undriven), .DIn(INSTR), .DOut(gate_8_1_dout));
  GATE_24 gate_24_6 (.EN(undriven), .DIn(SQC), .DOut(gate_24_6_dout));
  GATE_8 gate_8_2 (.EN(MOV_8), .DIn(INSTR), .DOut(gate_8_2_dout));
  GATE_8 gate_8_3 (.EN(LOAD_8), .DIn(INSTR), .DOut(gate_8_3_dout));
  GATE_8 gate_8_4 (.EN(SAVE_8), .DIn(INSTR), .DOut(gate_8_4_dout));
  GATE_8 gate_8_5 (.EN(SET_AB), .DIn(INSTR), .DOut(gate_8_5_dout));
  GATE_8 gate_8_6 (.EN(GOTO_16), .DIn(INSTR), .DOut(gate_8_6_dout));
  Pull_Resistor pull_resistor_1 (.node(gate_24_1_dout));
  Pull_Resistor pull_resistor_2 (.node(gate_8_2_dout));
  Pull_Resistor pull_resistor_3 (.node(gate_24_2_dout));
  Pull_Resistor pull_resistor_4 (.node(gate_24_3_dout));
  Pull_Resistor pull_resistor_5 (.node(gate_24_4_dout));
  Pull_Resistor pull_resistor_6 (.node(gate_24_5_dout));
  MOV8 mov8_1 (.SQC(gate_24_1_dout), .INSTR(gate_8_2_dout), .LOAD(mov8_1_load), .SEL(mov8_1_sel));
  LOAD load_1 (
    .INST(gate_8_3_dout), .SQC(gate_24_2_dout), .REG_LOAD(load_1_reg_load), .MSEL(load_1_msel),
    .PCSEL(load_1_pcsel), .MER(load_1_mer));
  SAVE save_1 (
    .INSTR(gate_8_4_dout), .SQC(gate_24_3_dout), .REG_SELECT(save_1_reg_select), .MSEL(save_1_msel),
    .PCSEL(save_1_pcsel), .MEW(MEW));
  setab setab_1 (.INSTR(gate_8_5_dout), .SQC(gate_24_4_dout), .A_LOAD(ALOAD), .B_LOAD(BLOAD), .DOut(DOut));
  GOTO goto_1 (
    .INSTR(gate_8_6_dout), .COND_REG(F), .SQC(gate_24_5_dout), .Sequence_Extra(Sequence_Extra),
    .J1LOAD(J1_LOAD), .M1LOAD(M1_LOAD), .J2LOAD(J2_LOAD), .M2LOAD(M2_LOAD), .MER(goto_1_mer),
    .INCLOAD(INC_LOAD), .JSEL(goto_1_jsel), .MSEL(goto_1_msel), .PCSEL(goto_1_pcsel), .PCLOAD(PC_LOAD),
    .INCSEL(INC_SEL));
  MOV_16 mov_16_1 (.Instructions(gate_8_1_dout), .SQC(gate_24_6_dout));  // open: M_LOAD, J_LOAD, XY_LOAD, J_SEL, XY_SEL
  _7432 #(.ShowInternalStructure("true")) u_7432_1 (
    .pin1(load_1_msel), .pin2(save_1_msel), .pin3(n7432_1_pin3), .pin4(n7432_1_pin3), .pin5(goto_1_msel),
    .pin6(M_SEL), .pin13(load_1_pcsel), .pin12(save_1_pcsel), .pin11(n7432_1_pin11), .pin10(n7432_1_pin11),
    .pin9(goto_1_pcsel), .pin8(PC_SEL));
  _7432 #(.ShowInternalStructure("true")) u_7432_2 (
    .pin1(load_1_mer), .pin2(goto_1_mer), .pin3(MER), .pin4(goto_1_jsel), .pin6(J_SEL));  // open: pin5, pin13, pin12, pin11, pin10, pin9, pin8
  GATE_8 gate_8_7 (.EN(MOV_8), .DIn(mov8_1_load), .DOut(gate_8_7_dout));
  GATE_8 gate_8_8 (.EN(LOAD_8), .DIn(load_1_reg_load), .DOut(gate_8_8_dout));
  OR_8 or_8_1 (.IN_1(gate_8_7_dout), .IN_2(gate_8_8_dout), .OUT_1(REG_LOAD));
  GATE_8 gate_8_9 (.EN(MOV_8), .DIn(mov8_1_sel), .DOut(gate_8_9_dout));
  GATE_8 gate_8_10 (.EN(SAVE_8), .DIn(save_1_reg_select), .DOut(gate_8_10_dout));
  OR_8 or_8_2 (.IN_1(gate_8_9_dout), .IN_2(gate_8_10_dout), .OUT_1(or_8_2_out_1));
  OR_8 or_8_3 (.IN_1(REG_IN), .IN_2(or_8_2_out_1), .OUT_1(REG_SELECT));

  assign AT_08 = 1'b1;
endmodule

module LOAD (
  input  [7:0] INST,
  input  [23:0] SQC,
  output [7:0] REG_LOAD,
  output MSEL,
  output PCSEL,
  output MER
);

  wire n7404_1_pin2, n7432_1_pin3, n7432_1_pin8, n7432_1_pin11, n74245_1_pin1;
  wire [2:2] pull_resistor_1_node;
  wire [7:0] threetoeight_1_o_111;

  Pull_Resistor pull_resistor_1 (.node(pull_resistor_1_node[2]));
  _7432 #(.ShowInternalStructure("true")) u_7432_1 (
    .pin1(SQC[8]), .pin2(SQC[7]), .pin3(n7432_1_pin3), .pin4(n7432_1_pin3), .pin5(SQC[6]), .pin6(MSEL),
    .pin12(SQC[7]), .pin11(n7432_1_pin11), .pin10(n7432_1_pin11), .pin9(SQC[6]), .pin8(n7432_1_pin8));  // open: pin13
  _7432 #(.ShowInternalStructure("true")) u_7432_2 (
    .pin13(SQC[10]), .pin12(SQC[9]), .pin11(PCSEL));  // open: pin1, pin2, pin3, pin4, pin5, pin6, pin10, pin9, pin8
  ThreeToEight threetoeight_1 (
    .FIn({pull_resistor_1_node[2], INST[1:0]}), .O_111(threetoeight_1_o_111[0]),
    .O_110(threetoeight_1_o_111[1]), .O_101(threetoeight_1_o_111[2]), .O_100(threetoeight_1_o_111[3]),
    .O_011(threetoeight_1_o_111[4]), .O_010(threetoeight_1_o_111[5]), .O_001(threetoeight_1_o_111[6]),
    .O_000(threetoeight_1_o_111[7]));
  _7404 #(.ShowInternalStructure("true")) u_7404_1 (
    .pin1(n7432_1_pin8), .pin2(n7404_1_pin2));  // open: pin3, pin4, pin5, pin6, pin13, pin12, pin11, pin10, pin9, pin8
  _74245 #(.ShowInternalStructure("true")) u_74245_1 (
    .pin1(n74245_1_pin1), .pin2(threetoeight_1_o_111[0]), .pin3(threetoeight_1_o_111[1]),
    .pin4(threetoeight_1_o_111[2]), .pin5(threetoeight_1_o_111[3]), .pin6(threetoeight_1_o_111[4]),
    .pin7(threetoeight_1_o_111[5]), .pin8(threetoeight_1_o_111[6]), .pin9(threetoeight_1_o_111[7]),
    .pin19(n7404_1_pin2), .pin18(REG_LOAD[0]), .pin17(REG_LOAD[1]), .pin16(REG_LOAD[2]), .pin15(REG_LOAD[3]),
    .pin14(REG_LOAD[4]), .pin13(REG_LOAD[5]), .pin12(REG_LOAD[6]), .pin11(REG_LOAD[7]));

  assign MER = SQC[7];
  // also tied to VCC on the sheet: n74245_1_pin1
endmodule

module SAVE (
  input  [7:0] INSTR,
  input  [23:0] SQC,
  output [7:0] REG_SELECT,
  output MSEL,
  output PCSEL,
  output MEW
);

  wire n7404_1_pin2, n7408_1_pin2, n7408_1_pin3, n7408_1_pin11, n7408_2_pin4, n7408_2_pin13, n7432_1_pin3,
       n7432_1_pin11, n74245_1_pin1;
  wire [7:0] n7408_2_pin11;

  _7408 #(.ShowInternalStructure("true")) u_7408_1 (
    .pin1(INSTR[1]), .pin2(n7408_1_pin2), .pin3(n7408_1_pin3), .pin13(n7408_1_pin2), .pin12(INSTR[0]),
    .pin11(n7408_1_pin11));  // open: pin4, pin5, pin6, pin10, pin9, pin8
  _7432 #(.ShowInternalStructure("true")) u_7432_1 (
    .pin1(SQC[7]), .pin2(SQC[8]), .pin3(n7432_1_pin3), .pin4(n7432_1_pin3), .pin5(SQC[6]), .pin6(MSEL),
    .pin13(SQC[8]), .pin12(SQC[7]), .pin11(n7432_1_pin11), .pin10(n7432_1_pin11), .pin9(SQC[6]),
    .pin8(n7408_1_pin2));
  _7432 #(.ShowInternalStructure("true")) u_7432_2 (
    .pin13(SQC[10]), .pin12(SQC[9]), .pin11(PCSEL));  // open: pin1, pin2, pin3, pin4, pin5, pin6, pin10, pin9, pin8
  _7408 #(.ShowInternalStructure("true")) u_7408_2 (
    .pin1(n7408_1_pin11), .pin2(n7408_1_pin3), .pin3(n7408_2_pin11[3]), .pin4(n7408_2_pin4),
    .pin5(n7408_1_pin11), .pin6(n7408_2_pin11[1]), .pin13(n7408_2_pin13), .pin12(n7408_2_pin4),
    .pin11(n7408_2_pin11[0]), .pin10(n7408_2_pin13), .pin9(n7408_1_pin3), .pin8(n7408_2_pin11[2]));
  Pull_Resistor pull_resistor_1 (.node(n7408_2_pin11[4]));
  Pull_Resistor pull_resistor_2 (.node(n7408_2_pin11[5]));
  Pull_Resistor pull_resistor_3 (.node(n7408_2_pin11[6]));
  Pull_Resistor pull_resistor_4 (.node(n7408_2_pin11[7]));
  _7404 #(.ShowInternalStructure("true")) u_7404_1 (
    .pin1(n7408_1_pin2), .pin2(n7404_1_pin2), .pin3(n7408_1_pin3), .pin4(n7408_2_pin4), .pin5(n7408_1_pin11),
    .pin6(n7408_2_pin13));  // open: pin13, pin12, pin11, pin10, pin9, pin8
  _74245 #(.ShowInternalStructure("true")) u_74245_1 (
    .pin1(n74245_1_pin1), .pin2(n7408_2_pin11[0]), .pin3(n7408_2_pin11[1]), .pin4(n7408_2_pin11[2]),
    .pin5(n7408_2_pin11[3]), .pin6(n7408_2_pin11[4]), .pin7(n7408_2_pin11[5]), .pin8(n7408_2_pin11[6]),
    .pin9(n7408_2_pin11[7]), .pin19(n7404_1_pin2), .pin18(REG_SELECT[0]), .pin17(REG_SELECT[1]),
    .pin16(REG_SELECT[2]), .pin15(REG_SELECT[3]), .pin14(REG_SELECT[4]), .pin13(REG_SELECT[5]),
    .pin12(REG_SELECT[6]), .pin11(REG_SELECT[7]));

  assign MEW = SQC[7];
  // also tied to VCC on the sheet: n74245_1_pin1
endmodule

module GATE_8 (
  input  EN,
  input  [7:0] DIn,
  output [7:0] DOut
);

  wire n7404_1_pin6, n74245_1_pin1;

  Pull_Resistor pull_resistor_1 (.node(DIn));
  _7404 #(.ShowInternalStructure("true")) u_7404_1 (
    .pin5(EN), .pin6(n7404_1_pin6));  // open: pin1, pin2, pin3, pin4, pin13, pin12, pin11, pin10, pin9, pin8
  _74245 #(.ShowInternalStructure("true")) u_74245_1 (
    .pin1(n74245_1_pin1), .pin2(DIn[0]), .pin3(DIn[1]), .pin4(DIn[2]), .pin5(DIn[3]), .pin6(DIn[4]),
    .pin7(DIn[5]), .pin8(DIn[6]), .pin9(DIn[7]), .pin19(n7404_1_pin6), .pin18(DOut[0]), .pin17(DOut[1]),
    .pin16(DOut[2]), .pin15(DOut[3]), .pin14(DOut[4]), .pin13(DOut[5]), .pin12(DOut[6]), .pin11(DOut[7]));
  Pull_Resistor pull_resistor_2 (.node(DOut));
  // also tied to VCC on the sheet: n74245_1_pin1
endmodule

module GATE_24 (
  input  EN,
  input  [23:0] DIn,
  output [23:0] DOut
);

  wire n7404_1_pin6, n74245_1_pin1, n74245_2_pin1, n74245_3_pin1;

  _7404 #(.ShowInternalStructure("true")) u_7404_1 (
    .pin5(EN), .pin6(n7404_1_pin6));  // open: pin1, pin2, pin3, pin4, pin13, pin12, pin11, pin10, pin9, pin8
  _74245 #(.ShowInternalStructure("true")) u_74245_1 (
    .pin1(n74245_1_pin1), .pin2(DIn[0]), .pin3(DIn[1]), .pin4(DIn[2]), .pin5(DIn[3]), .pin6(DIn[4]),
    .pin7(DIn[5]), .pin8(DIn[6]), .pin9(DIn[7]), .pin19(n7404_1_pin6), .pin18(DOut[0]), .pin17(DOut[1]),
    .pin16(DOut[2]), .pin15(DOut[3]), .pin14(DOut[4]), .pin13(DOut[5]), .pin12(DOut[6]), .pin11(DOut[7]));
  _74245 #(.ShowInternalStructure("true")) u_74245_2 (
    .pin1(n74245_2_pin1), .pin2(DIn[8]), .pin3(DIn[9]), .pin4(DIn[10]), .pin5(DIn[11]), .pin6(DIn[12]),
    .pin7(DIn[13]), .pin8(DIn[14]), .pin9(DIn[15]), .pin19(n7404_1_pin6), .pin18(DOut[8]), .pin17(DOut[9]),
    .pin16(DOut[10]), .pin15(DOut[11]), .pin14(DOut[12]), .pin13(DOut[13]), .pin12(DOut[14]), .pin11(DOut[15]));
  _74245 #(.ShowInternalStructure("true")) u_74245_3 (
    .pin1(n74245_3_pin1), .pin2(DIn[16]), .pin3(DIn[17]), .pin4(DIn[18]), .pin5(DIn[19]), .pin6(DIn[20]),
    .pin7(DIn[21]), .pin8(DIn[22]), .pin9(DIn[23]), .pin19(n7404_1_pin6), .pin18(DOut[16]), .pin17(DOut[17]),
    .pin16(DOut[18]), .pin15(DOut[19]), .pin14(DOut[20]), .pin13(DOut[21]), .pin12(DOut[22]), .pin11(DOut[23]));
  // also tied to VCC on the sheet: {n74245_1_pin1, n74245_2_pin1, n74245_3_pin1}
endmodule

module setab (
  input  [7:0] INSTR,
  input  [23:0] SQC,
  output A_LOAD,
  output B_LOAD,
  output [7:0] DOut
);

  wire n7404_1_pin8, n7432_1_pin8, n7432_1_pin11;

  _7404 #(.ShowInternalStructure("true")) u_7404_1 (
    .pin9(INSTR[5]), .pin8(n7404_1_pin8));  // open: pin1, pin2, pin3, pin4, pin5, pin6, pin13, pin12, pin11, pin10
  _7432 #(.ShowInternalStructure("true")) u_7432_1 (
    .pin13(SQC[9]), .pin12(SQC[8]), .pin11(n7432_1_pin11), .pin10(n7432_1_pin11), .pin9(SQC[7]),
    .pin8(n7432_1_pin8));  // open: pin1, pin2, pin3, pin4, pin5, pin6
  _7408 #(.ShowInternalStructure("true")) u_7408_1 (
    .pin13(n7404_1_pin8), .pin12(SQC[8]), .pin11(A_LOAD), .pin10(INSTR[5]), .pin9(SQC[8]), .pin8(B_LOAD));  // open: pin1, pin2, pin3, pin4, pin5, pin6
  GATE_8 gate_8_1 (.EN(n7432_1_pin8), .DIn({INSTR[0], INSTR[1], INSTR[2], INSTR[3], {4{INSTR[4]}}}), .DOut(DOut));
endmodule

module GOTO (
  input  [7:0] INSTR,
  input  [2:0] COND_REG,
  input  [23:0] SQC,
  input  [15:0] Sequence_Extra,
  output J1LOAD,
  output M1LOAD,
  output J2LOAD,
  output M2LOAD,
  output MER,
  output INCLOAD,
  output JSEL,
  output MSEL,
  output PCSEL,
  output PCLOAD,
  output INCSEL
);

  wire n7404_1_pin2, n7404_1_pin3, n7404_1_pin4, n7404_1_pin5, n7404_1_pin6, n7404_1_pin8, n7404_1_pin9,
       n7404_1_pin10, n7404_1_pin11, n7404_1_pin12, n7404_2_pin8, n7404_2_pin10, n7404_2_pin12, n7404_3_pin2,
       n7404_3_pin4, n7404_3_pin6, n7404_3_pin8, n7404_3_pin12, n7408_1_pin1, n7408_1_pin3, n7408_1_pin5,
       n7408_1_pin6, n7408_1_pin8, n7408_1_pin11, n7408_1_pin12, n7408_2_pin3, n7408_2_pin6, n7408_2_pin8,
       n7408_2_pin11, n7408_4_pin3, n7408_4_pin6, n7408_4_pin11, n7408_5_pin6, n7408_6_pin3, n7408_6_pin6,
       n7408_6_pin8, n7408_6_pin11, n7408_9_pin3, n7408_9_pin6, n7408_9_pin8, n7408_9_pin11, n7432_1_pin3,
       n7432_1_pin6, n7432_1_pin8, n7432_1_pin11, n7432_2_pin3, n7432_2_pin6, n7432_3_pin3, n7432_3_pin6,
       n7432_3_pin8, n7432_3_pin11, n7432_4_pin3, n7432_4_pin6, n7432_4_pin8, n7432_4_pin11, n7432_5_pin3,
       n7432_5_pin4, n7432_5_pin11, n7432_6_pin2, n7432_6_pin3, n7432_6_pin4, n7432_6_pin5, n7432_6_pin6,
       n7432_6_pin11, n7432_7_pin3, n7432_8_pin12, n7432_10_pin6, n7432_10_pin8, n7432_10_pin11,
       n7432_11_pin5, n7432_11_pin6, n7432_12_pin3, n7432_12_pin6;
  wire [7:0] dual_regist_b_c_1_bout;

  _7432 #(.ShowInternalStructure("true")) u_7432_1 (
    .pin1(SQC[5]), .pin2(SQC[6]), .pin3(n7432_1_pin3), .pin4(n7432_1_pin3), .pin5(SQC[7]),
    .pin6(n7432_1_pin6), .pin13(SQC[5]), .pin12(SQC[6]), .pin11(n7432_1_pin11), .pin10(n7432_1_pin11),
    .pin9(SQC[7]), .pin8(n7432_1_pin8));
  _7408 #(.ShowInternalStructure("true")) u_7408_1 (
    .pin1(n7408_1_pin1), .pin2(Sequence_Extra[1]), .pin3(n7408_1_pin3), .pin4(n7408_1_pin1),
    .pin5(n7408_1_pin5), .pin6(n7408_1_pin6), .pin13(n7408_1_pin1), .pin12(n7408_1_pin12),
    .pin11(n7408_1_pin11), .pin10(n7408_1_pin1), .pin9(Sequence_Extra[4]), .pin8(n7408_1_pin8));
  _7432 #(.ShowInternalStructure("true")) u_7432_2 (
    .pin1(Sequence_Extra[0]), .pin2(Sequence_Extra[2]), .pin3(n7432_2_pin3), .pin4(Sequence_Extra[3]),
    .pin5(Sequence_Extra[5]), .pin6(n7432_2_pin6), .pin13(Sequence_Extra[1]), .pin12(n7432_2_pin3),
    .pin11(n7408_1_pin12), .pin10(Sequence_Extra[4]), .pin9(n7432_2_pin6), .pin8(n7408_1_pin5));
  _7432 #(.ShowInternalStructure("true")) u_7432_3 (
    .pin1(SQC[11]), .pin2(SQC[12]), .pin3(n7432_3_pin3), .pin4(SQC[13]), .pin5(SQC[14]), .pin6(n7432_3_pin6),
    .pin13(SQC[8]), .pin12(SQC[9]), .pin11(n7432_3_pin11), .pin10(n7432_3_pin11), .pin9(SQC[10]),
    .pin8(n7432_3_pin8));
  _7404 #(.ShowInternalStructure("true")) u_7404_1 (
    .pin1(dual_regist_b_c_1_bout[5]), .pin2(n7404_1_pin2), .pin3(n7404_1_pin3), .pin4(n7404_1_pin4),
    .pin5(n7404_1_pin5), .pin6(n7404_1_pin6), .pin13(COND_REG[2]), .pin12(n7404_1_pin12),
    .pin11(n7404_1_pin11), .pin10(n7404_1_pin10), .pin9(n7404_1_pin9), .pin8(n7404_1_pin8));
  _7432 #(.ShowInternalStructure("true")) u_7432_4 (
    .pin1(n7432_3_pin6), .pin2(SQC[15]), .pin3(n7432_4_pin3), .pin4(SQC[16]), .pin5(SQC[17]),
    .pin6(n7432_4_pin6), .pin13(SQC[13]), .pin12(SQC[14]), .pin11(n7432_4_pin11), .pin10(n7432_4_pin11),
    .pin9(SQC[15]), .pin8(n7432_4_pin8));
  _7432 #(.ShowInternalStructure("true")) u_7432_5 (
    .pin1(n7432_4_pin6), .pin2(SQC[18]), .pin3(n7432_5_pin3), .pin4(n7432_5_pin4), .pin5(SQC[23]),
    .pin13(SQC[19]), .pin12(SQC[20]), .pin11(n7432_5_pin11), .pin10(SQC[21]), .pin9(SQC[22]),
    .pin8(n7432_5_pin4));  // open: pin6
  Dual_Regist_B_C dual_regist_b_c_1 (
    .DIn(INSTR), .CLK(SQC[5]), .LOAD1(SQC[5]), .BOut(dual_regist_b_c_1_bout));  // open: LOAD2, SELECT1, SELECT2, LOAD12, SELECT12, D16In, COut, D16Out
  _7408 #(.ShowInternalStructure("true")) u_7408_2 (
    .pin1(dual_regist_b_c_1_bout[1]), .pin2(COND_REG[0]), .pin3(n7408_2_pin3),
    .pin4(dual_regist_b_c_1_bout[2]), .pin5(n7404_1_pin3), .pin6(n7408_2_pin6),
    .pin13(dual_regist_b_c_1_bout[4]), .pin12(n7404_1_pin11), .pin11(n7408_2_pin11),
    .pin10(dual_regist_b_c_1_bout[3]), .pin9(n7404_1_pin9), .pin8(n7408_2_pin8));
  _7404 #(.ShowInternalStructure("true")) u_7404_2 (
    .pin13(COND_REG[1]), .pin12(n7404_2_pin12), .pin11(COND_REG[2]), .pin10(n7404_2_pin10),
    .pin9(COND_REG[0]), .pin8(n7404_2_pin8));  // open: pin1, pin2, pin3, pin4, pin5, pin6
  _7408 #(.ShowInternalStructure("true")) u_7408_3 (
    .pin1(COND_REG[1]), .pin2(dual_regist_b_c_1_bout[4]), .pin3(n7404_1_pin11), .pin4(COND_REG[0]),
    .pin5(dual_regist_b_c_1_bout[3]), .pin6(n7404_1_pin9), .pin13(dual_regist_b_c_1_bout[2]),
    .pin12(COND_REG[2]), .pin11(n7404_1_pin3), .pin10(dual_regist_b_c_1_bout[1]), .pin9(n7404_1_pin12),
    .pin8(n7404_1_pin5));
  _7408 #(.ShowInternalStructure("true")) u_7408_4 (
    .pin1(n7404_1_pin10), .pin2(n7404_1_pin8), .pin3(n7408_4_pin3), .pin4(n7408_4_pin3), .pin5(n7404_1_pin4),
    .pin6(n7408_4_pin6), .pin13(n7408_4_pin6), .pin12(n7404_1_pin6), .pin11(n7408_4_pin11));  // open: pin10, pin9, pin8
  _7404 #(.ShowInternalStructure("true")) u_7404_3 (
    .pin1(dual_regist_b_c_1_bout[3]), .pin2(n7404_3_pin2), .pin3(dual_regist_b_c_1_bout[2]),
    .pin4(n7404_3_pin4), .pin5(dual_regist_b_c_1_bout[0]), .pin6(n7404_3_pin6),
    .pin13(dual_regist_b_c_1_bout[4]), .pin12(n7404_3_pin12), .pin9(dual_regist_b_c_1_bout[1]),
    .pin8(n7404_3_pin8));  // open: pin11, pin10
  _7432 #(.ShowInternalStructure("true")) u_7432_6 (
    .pin1(dual_regist_b_c_1_bout[0]), .pin2(n7432_6_pin2), .pin3(n7432_6_pin3), .pin4(n7432_6_pin4),
    .pin5(n7432_6_pin5), .pin6(n7432_6_pin6), .pin13(n7408_2_pin3), .pin12(n7408_2_pin6),
    .pin11(n7432_6_pin11), .pin10(n7432_6_pin11), .pin8(n7432_6_pin5));  // open: pin9
  _7408 #(.ShowInternalStructure("true")) u_7408_5 (
    .pin4(n7404_2_pin8), .pin5(dual_regist_b_c_1_bout[3]), .pin6(n7408_5_pin6), .pin13(n7408_2_pin11),
    .pin12(n7404_2_pin12), .pin11(n7432_6_pin4), .pin10(n7404_1_pin3), .pin9(n7404_2_pin10),
    .pin8(n7432_6_pin2));  // open: pin1, pin2, pin3
  _7408 #(.ShowInternalStructure("true")) u_7408_6 (
    .pin1(n7404_3_pin12), .pin2(n7404_3_pin2), .pin3(n7408_6_pin3), .pin4(n7408_6_pin3), .pin5(n7404_3_pin4),
    .pin6(n7408_6_pin6), .pin13(n7408_6_pin6), .pin12(n7404_3_pin6), .pin11(n7408_6_pin11),
    .pin10(n7408_6_pin11), .pin9(n7404_3_pin8), .pin8(n7408_6_pin8));
  _7432 #(.ShowInternalStructure("true")) u_7432_7 (
    .pin1(n7432_6_pin6), .pin2(n7408_6_pin8), .pin3(n7432_7_pin3), .pin4(n7432_7_pin3), .pin5(n7408_5_pin6),
    .pin6(n7408_1_pin1));  // open: pin13, pin12, pin11, pin10, pin9, pin8
  _7432 #(.ShowInternalStructure("true")) u_7432_8 (
    .pin13(n7408_1_pin11), .pin12(n7432_8_pin12), .pin11(PCSEL));  // open: pin1, pin2, pin3, pin4, pin5, pin6, pin10, pin9, pin8
  _7432 #(.ShowInternalStructure("true")) u_7432_9 (
    .pin10(n7408_1_pin3), .pin9(SQC[9]), .pin8(INCLOAD));  // open: pin1, pin2, pin3, pin4, pin5, pin6, pin13, pin12, pin11
  _7408 #(.ShowInternalStructure("true")) u_7408_7 (
    .pin1(SQC[6]), .pin2(dual_regist_b_c_1_bout[5]), .pin3(J1LOAD), .pin4(SQC[6]), .pin5(n7404_1_pin2),
    .pin6(M1LOAD), .pin13(dual_regist_b_c_1_bout[5]), .pin12(SQC[14]), .pin11(J2LOAD), .pin10(n7404_1_pin2),
    .pin9(SQC[14]), .pin8(M2LOAD));
  _7432 #(.ShowInternalStructure("true")) u_7432_10 (
    .pin1(n7432_1_pin6), .pin2(n7432_4_pin8), .pin3(MER), .pin4(SQC[11]), .pin5(SQC[17]),
    .pin6(n7432_10_pin6), .pin13(n7432_1_pin8), .pin12(n7432_3_pin8), .pin11(n7432_10_pin11),
    .pin10(n7432_5_pin3), .pin9(n7432_3_pin3), .pin8(n7432_10_pin8));
  _7432 #(.ShowInternalStructure("true")) u_7432_11 (
    .pin4(n7432_10_pin6), .pin5(n7432_11_pin5), .pin6(n7432_11_pin6), .pin13(n7432_10_pin11),
    .pin12(n7432_4_pin3), .pin11(n7432_8_pin12), .pin10(n7432_10_pin8), .pin9(n7408_1_pin6), .pin8(INCSEL));  // open: pin1, pin2, pin3
  _7408 #(.ShowInternalStructure("true")) u_7408_8 (
    .pin1(n7404_1_pin2), .pin2(n7432_5_pin11), .pin3(MSEL), .pin4(dual_regist_b_c_1_bout[5]),
    .pin5(n7432_5_pin11), .pin6(JSEL), .pin9(n7408_4_pin11));  // open: pin13, pin12, pin11, pin10, pin8
  _7408 #(.ShowInternalStructure("true")) u_7408_9 (
    .pin1(SQC[19]), .pin2(n7432_6_pin3), .pin3(n7408_9_pin3), .pin4(SQC[19]), .pin5(n7404_1_pin5),
    .pin6(n7408_9_pin6), .pin13(n7404_1_pin9), .pin12(SQC[19]), .pin11(n7408_9_pin11), .pin10(SQC[19]),
    .pin9(n7404_1_pin11), .pin8(n7408_9_pin8));
  _7432 #(.ShowInternalStructure("true")) u_7432_12 (
    .pin1(n7408_9_pin6), .pin2(n7408_9_pin3), .pin3(n7432_12_pin3), .pin4(n7432_12_pin3),
    .pin5(n7408_9_pin11), .pin6(n7432_12_pin6), .pin13(n7432_12_pin6), .pin12(n7408_9_pin8),
    .pin11(n7432_11_pin5), .pin10(n7432_11_pin6), .pin9(n7408_1_pin8), .pin8(PCLOAD));
endmodule

module OR_8 (
  input  [7:0] IN_1,
  input  [7:0] IN_2,
  output [7:0] OUT_1
);

  Pull_Resistor pull_resistor_1 (.node(IN_1));
  _7432 #(.ShowInternalStructure("true")) u_7432_1 (
    .pin1(IN_1[0]), .pin2(IN_2[0]), .pin3(OUT_1[0]), .pin4(IN_1[1]), .pin5(IN_2[1]), .pin6(OUT_1[1]),
    .pin13(IN_1[2]), .pin12(IN_2[2]), .pin11(OUT_1[2]), .pin10(IN_1[3]), .pin9(IN_2[3]), .pin8(OUT_1[3]));
  _7432 #(.ShowInternalStructure("true")) u_7432_2 (
    .pin1(IN_1[4]), .pin2(IN_2[4]), .pin3(OUT_1[4]), .pin4(IN_1[5]), .pin5(IN_2[5]), .pin6(OUT_1[5]),
    .pin13(IN_1[6]), .pin12(IN_2[6]), .pin11(OUT_1[6]), .pin10(IN_1[7]), .pin9(IN_2[7]), .pin8(OUT_1[7]));
endmodule

module Testbett (
);

  wire CLK_T, cpu_shared_1_free, CPUEN_B, D_PEND, D_RUN, EN_A, EN_B, FORK_REQ_A, GRANT_A, GRANT_B, HI,
       nCLK_T, nRUN_B, or_1_out, PEND, PIN_B, REQ_A, REQ_B, RUN_B, WE_BUS_A, WE_BUS_B;
  wire [7:0] DATA_FROM_RAM, DATA_TO_RAM;
  wire [15:0] ADDR_BUS, FORK_ADDR_A;

  _7404 #(.ShowInternalStructure("true")) u_7404_1 (
    .pin1(CLK_T), .pin2(nCLK_T));  // open: pin3, pin4, pin5, pin6, pin13, pin12, pin11, pin10, pin9, pin8
  or or_1 (or_1_out, WE_BUS_A, WE_BUS_B);
  RAM #(.addrWidth(16), .enables("line"), .\type ("nonvolatile")) ram_1 (
    .addr(ADDR_BUS), .we(or_1_out), .clk(CLK_T), .din(DATA_TO_RAM), .dout(DATA_FROM_RAM));
  Clock clock_1 (.out(CLK_T));
  _7474 #(.ShowInternalStructure("true")) u_7474_1 (
    .pin1(HI), .pin2(D_PEND), .pin3(nCLK_T), .pin4(HI), .pin5(PEND), .pin13(HI), .pin12(D_RUN),
    .pin11(nCLK_T), .pin10(HI), .pin9(RUN_B), .pin8(nRUN_B));  // open: pin6
  CPU_SHARED cpu_shared_1 (
    .CPU_ENABLE(1'b1), .Data_In(DATA_FROM_RAM), .EN(EN_A), .GRANT(GRANT_A), .FORK_LOAD(1'b0),
    .FORK_ADDR_IN({16{1'b0}}), .CPU_ID({8{1'b0}}), .FREE(cpu_shared_1_free), .Adress_Bus(ADDR_BUS),
    .Write_en(WE_BUS_A), .Data_Out(DATA_TO_RAM), .BUS_REQ(REQ_A), .FORK_REQ(FORK_REQ_A),
    .FORK_ADDR(FORK_ADDR_A));  // open: Sequnce
  CPU_SHARED cpu_shared_2 (
    .CPU_ENABLE(CPUEN_B), .Data_In(DATA_FROM_RAM), .EN(EN_B), .GRANT(GRANT_B), .FORK_LOAD(PEND),
    .FORK_ADDR_IN(FORK_ADDR_A), .CPU_ID(8'h1), .Adress_Bus(ADDR_BUS), .Write_en(WE_BUS_B),
    .Data_Out(DATA_TO_RAM), .BUS_REQ(REQ_B));  // open: Sequnce, FREE, FORK_REQ, FORK_ADDR
  _7408 #(.ShowInternalStructure("true")) u_7408_1 (
    .pin1(FORK_REQ_A), .pin2(nRUN_B), .pin3(D_PEND), .pin4(PIN_B), .pin5(RUN_B), .pin6(CPUEN_B));  // open: pin13, pin12, pin11, pin10, pin9, pin8
  Pull_Resistor pull_resistor_1 (.node(DATA_FROM_RAM));
  _7432 #(.ShowInternalStructure("true")) u_7432_1 (
    .pin1(PEND), .pin2(RUN_B), .pin3(D_RUN));  // open: pin4, pin5, pin6, pin13, pin12, pin11, pin10, pin9, pin8
  BUS_ARBITER bus_arbiter_1 (
    .CLK(CLK_T), .REQ_A(REQ_A), .REQ_B(REQ_B), .GRANT_A(GRANT_A), .GRANT_B(GRANT_B), .EN_A(EN_A), .EN_B(EN_B));  // open: O
  // also tied to VCC on the sheet: {HI, PIN_B}
endmodule

module Conv_16_to_14 (
  input  [15:0] IN_0,
  output [13:0] OUT_0
);


  assign OUT_0 = IN_0[13:0];
endmodule

module OUT_8 (
  input  [7:0] INSTR,
  input  [23:0] SQC,
  output [7:0] REG_SELECT,
  output OUT8
);

  wire n7432_1_pin3, n7432_1_pin6;
  wire [2:1] pull_resistor_3_node;
  wire [7:0] threetoeight_1_o_000;

  Pull_Resistor pull_resistor_1 (.node(pull_resistor_3_node[2]));
  Pull_Resistor pull_resistor_2 (.node(SQC));
  Pull_Resistor pull_resistor_3 (.node(pull_resistor_3_node[1]));
  _7432 #(.ShowInternalStructure("true")) u_7432_1 (
    .pin1(SQC[8]), .pin2(SQC[7]), .pin3(n7432_1_pin3), .pin4(n7432_1_pin3), .pin5(SQC[6]), .pin6(n7432_1_pin6));  // open: pin13, pin12, pin11, pin10, pin9, pin8
  ThreeToEight threetoeight_1 (
    .FIn({pull_resistor_3_node, INSTR[0]}), .O_001(threetoeight_1_o_000[3]), .O_000(threetoeight_1_o_000[0]));  // open: O_111, O_110, O_101, O_100, O_011, O_010
  Pull_Resistor pull_resistor_4 (.node(threetoeight_1_o_000[1]));
  Pull_Resistor pull_resistor_5 (.node(threetoeight_1_o_000[2]));
  Pull_Resistor pull_resistor_6 (.node(threetoeight_1_o_000[4]));
  Pull_Resistor pull_resistor_7 (.node(threetoeight_1_o_000[5]));
  Pull_Resistor pull_resistor_8 (.node(threetoeight_1_o_000[6]));
  Pull_Resistor pull_resistor_9 (.node(threetoeight_1_o_000[7]));
  GATE_8 gate_8_1 (.EN(n7432_1_pin6), .DIn(threetoeight_1_o_000), .DOut(REG_SELECT));

  assign OUT8 = SQC[7];
endmodule

module Output_Register (
  input  [7:0] DIn,
  input  CLK,
  input  OUT8,
  input  [7:0] INSTR,
  input  [23:0] SQC,
  output [7:0] DISP_OUT,
  output [7:0] REG_SELECT
);

  wire n7432_1_pin1, n7432_1_pin2, n7432_1_pin3, n7432_1_pin5, n74245_1_pin1, n74245_1_pin19, n74273_1_pin11,
       out_8_1_out8;
  wire [7:0] gate_8_1_dout, n74245_1_pin18;
  wire [23:0] gate_24_1_dout;

  GATE_8 gate_8_1 (.EN(OUT8), .DIn(INSTR), .DOut(gate_8_1_dout));
  GATE_24 gate_24_1 (.EN(OUT8), .DIn(SQC), .DOut(gate_24_1_dout));
  OUT_8 out_8_1 (.INSTR(gate_8_1_dout), .SQC(gate_24_1_dout), .REG_SELECT(REG_SELECT), .OUT8(out_8_1_out8));
  _74245 #(.ShowInternalStructure("true")) u_74245_1 (
    .pin1(n74245_1_pin1), .pin2(DIn[0]), .pin3(DIn[1]), .pin4(DIn[2]), .pin5(DIn[3]), .pin6(DIn[4]),
    .pin7(DIn[5]), .pin8(DIn[6]), .pin9(DIn[7]), .pin19(n74245_1_pin19), .pin18(n74245_1_pin18[0]),
    .pin17(n74245_1_pin18[1]), .pin16(n74245_1_pin18[2]), .pin15(n74245_1_pin18[3]),
    .pin14(n74245_1_pin18[4]), .pin13(n74245_1_pin18[5]), .pin12(n74245_1_pin18[6]), .pin11(n74245_1_pin18[7]));
  Pull_Resistor pull_resistor_1 (.node(n74245_1_pin18));
  _7404 #(.ShowInternalStructure("true")) u_7404_1 (
    .pin11(out_8_1_out8), .pin10(n74245_1_pin19));  // open: pin1, pin2, pin3, pin4, pin5, pin6, pin13, pin12, pin9, pin8
  _74273 #(.ShowInternalStructure("true")) u_74273_1 (
    .pin2(DISP_OUT[0]), .pin3(n74245_1_pin18[0]), .pin4(n74245_1_pin18[1]), .pin5(DISP_OUT[1]),
    .pin6(DISP_OUT[2]), .pin7(n74245_1_pin18[2]), .pin8(n74245_1_pin18[3]), .pin9(DISP_OUT[3]),
    .pin19(DISP_OUT[7]), .pin18(n74245_1_pin18[7]), .pin17(n74245_1_pin18[6]), .pin16(DISP_OUT[6]),
    .pin15(DISP_OUT[5]), .pin14(n74245_1_pin18[5]), .pin13(n74245_1_pin18[4]), .pin12(DISP_OUT[4]),
    .pin11(n74273_1_pin11));  // open: pin1
  _7432 #(.ShowInternalStructure("true")) u_7432_1 (
    .pin1(n7432_1_pin1), .pin2(n7432_1_pin2), .pin3(n7432_1_pin3), .pin4(n7432_1_pin2), .pin5(n7432_1_pin5),
    .pin6(n74273_1_pin11));  // open: pin13, pin12, pin11, pin10, pin9, pin8
  _7408 #(.ShowInternalStructure("true")) u_7408_1 (
    .pin1(out_8_1_out8), .pin2(CLK), .pin3(n7432_1_pin5), .pin4(CLK), .pin6(n7432_1_pin1), .pin12(CLK),
    .pin11(n7432_1_pin2));  // open: pin5, pin13, pin10, pin9, pin8
  // also tied to VCC on the sheet: n74245_1_pin1
endmodule

module Dual_Register_A_D (
  input  [7:0] DIn,
  input  CLK,
  input  LOAD1,
  input  LOAD2,
  input  SELECT1,
  input  SELECT2,
  input  LOAD12,
  input  SELECT12,
  input  [15:0] D16In,
  output [7:0] DOut,
  output [15:0] D16Out
);

  wire n7404_1_pin2, n7404_1_pin4, n7404_1_pin6, n7404_1_pin8, n7404_1_pin12, n7432_1_pin1, n7432_1_pin2,
       n7432_1_pin3, n7432_1_pin5, n74245_1_pin1, n74245_1_pin19, n74245_2_pin1, n74245_3_pin1,
       n74245_4_pin1, n74245_5_pin1, n74245_6_pin1, n74245_7_pin1, n74245_8_pin1, n74273_1_pin11;
  wire [7:0] n74245_1_pin11, n74245_3_pin18, n74273_1_pin19, n74273_2_pin2;

  _74245 #(.ShowInternalStructure("true")) u_74245_1 (
    .pin1(n74245_1_pin1), .pin2(DIn[0]), .pin3(DIn[1]), .pin4(DIn[2]), .pin5(DIn[3]), .pin6(DIn[4]),
    .pin7(DIn[5]), .pin8(DIn[6]), .pin9(DIn[7]), .pin19(n74245_1_pin19), .pin18(n74245_1_pin11[7]),
    .pin17(n74245_1_pin11[6]), .pin16(n74245_1_pin11[5]), .pin15(n74245_1_pin11[4]),
    .pin14(n74245_1_pin11[3]), .pin13(n74245_1_pin11[2]), .pin12(n74245_1_pin11[1]), .pin11(n74245_1_pin11[0]));
  Pull_Resistor pull_resistor_1 (.node(n74245_1_pin11));
  _7404 #(.ShowInternalStructure("true")) u_7404_1 (
    .pin1(SELECT2), .pin2(n7404_1_pin2), .pin3(SELECT12), .pin4(n7404_1_pin4), .pin5(LOAD12),
    .pin6(n7404_1_pin6), .pin13(SELECT1), .pin12(n7404_1_pin12), .pin11(LOAD1), .pin10(n74245_1_pin19),
    .pin9(LOAD2), .pin8(n7404_1_pin8));
  _74245 #(.ShowInternalStructure("true")) u_74245_2 (
    .pin1(n74245_2_pin1), .pin2(D16In[0]), .pin3(D16In[1]), .pin4(D16In[2]), .pin5(D16In[3]),
    .pin6(D16In[4]), .pin7(D16In[5]), .pin8(D16In[6]), .pin9(D16In[7]), .pin19(n7404_1_pin6),
    .pin18(n74245_1_pin11[0]), .pin17(n74245_1_pin11[1]), .pin16(n74245_1_pin11[2]),
    .pin15(n74245_1_pin11[3]), .pin14(n74245_1_pin11[4]), .pin13(n74245_1_pin11[5]),
    .pin12(n74245_1_pin11[6]), .pin11(n74245_1_pin11[7]));
  _74245 #(.ShowInternalStructure("true")) u_74245_3 (
    .pin1(n74245_3_pin1), .pin2(D16In[8]), .pin3(D16In[9]), .pin4(D16In[10]), .pin5(D16In[11]),
    .pin6(D16In[12]), .pin7(D16In[13]), .pin8(D16In[14]), .pin9(D16In[15]), .pin19(n7404_1_pin6),
    .pin18(n74245_3_pin18[0]), .pin17(n74245_3_pin18[1]), .pin16(n74245_3_pin18[2]),
    .pin15(n74245_3_pin18[3]), .pin14(n74245_3_pin18[4]), .pin13(n74245_3_pin18[5]),
    .pin12(n74245_3_pin18[6]), .pin11(n74245_3_pin18[7]));
  _74273 #(.ShowInternalStructure("true")) u_74273_1 (
    .pin2(n74273_1_pin19[7]), .pin3(n74245_1_pin11[0]), .pin4(n74245_1_pin11[1]), .pin5(n74273_1_pin19[6]),
    .pin6(n74273_1_pin19[5]), .pin7(n74245_1_pin11[2]), .pin8(n74245_1_pin11[3]), .pin9(n74273_1_pin19[4]),
    .pin19(n74273_1_pin19[0]), .pin18(n74245_1_pin11[7]), .pin17(n74245_1_pin11[6]),
    .pin16(n74273_1_pin19[1]), .pin15(n74273_1_pin19[2]), .pin14(n74245_1_pin11[5]),
    .pin13(n74245_1_pin11[4]), .pin12(n74273_1_pin19[3]), .pin11(n74273_1_pin11));  // open: pin1
  _7432 #(.ShowInternalStructure("true")) u_7432_1 (
    .pin1(n7432_1_pin1), .pin2(n7432_1_pin2), .pin3(n7432_1_pin3), .pin4(n7432_1_pin2), .pin5(n7432_1_pin5),
    .pin6(n74273_1_pin11));  // open: pin13, pin12, pin11, pin10, pin9, pin8
  _7408 #(.ShowInternalStructure("true")) u_7408_1 (
    .pin1(LOAD1), .pin2(CLK), .pin3(n7432_1_pin5), .pin4(CLK), .pin5(LOAD2), .pin6(n7432_1_pin1),
    .pin13(LOAD12), .pin12(CLK), .pin11(n7432_1_pin2));  // open: pin10, pin9, pin8
  _74245 #(.ShowInternalStructure("true")) u_74245_4 (
    .pin1(n74245_4_pin1), .pin2(DIn[7]), .pin3(DIn[6]), .pin4(DIn[5]), .pin5(DIn[4]), .pin6(DIn[3]),
    .pin7(DIn[2]), .pin8(DIn[1]), .pin9(DIn[0]), .pin19(n7404_1_pin8), .pin18(n74245_3_pin18[0]),
    .pin17(n74245_3_pin18[1]), .pin16(n74245_3_pin18[2]), .pin15(n74245_3_pin18[3]),
    .pin14(n74245_3_pin18[4]), .pin13(n74245_3_pin18[5]), .pin12(n74245_3_pin18[6]), .pin11(n74245_3_pin18[7]));
  Pull_Resistor pull_resistor_2 (.node(n74245_3_pin18));
  _74273 #(.ShowInternalStructure("true")) u_74273_2 (
    .pin2(n74273_2_pin2[0]), .pin3(n74245_3_pin18[0]), .pin4(n74245_3_pin18[1]), .pin5(n74273_2_pin2[1]),
    .pin6(n74273_2_pin2[2]), .pin7(n74245_3_pin18[2]), .pin8(n74245_3_pin18[3]), .pin9(n74273_2_pin2[3]),
    .pin19(n74273_2_pin2[7]), .pin18(n74245_3_pin18[7]), .pin17(n74245_3_pin18[6]), .pin16(n74273_2_pin2[6]),
    .pin15(n74273_2_pin2[5]), .pin14(n74245_3_pin18[5]), .pin13(n74245_3_pin18[4]), .pin12(n74273_2_pin2[4]),
    .pin11(n7432_1_pin3));  // open: pin1
  _74245 #(.ShowInternalStructure("true")) u_74245_5 (
    .pin1(n74245_5_pin1), .pin2(n74273_1_pin19[7]), .pin3(n74273_1_pin19[6]), .pin4(n74273_1_pin19[5]),
    .pin5(n74273_1_pin19[4]), .pin6(n74273_1_pin19[3]), .pin7(n74273_1_pin19[2]), .pin8(n74273_1_pin19[1]),
    .pin9(n74273_1_pin19[0]), .pin19(n7404_1_pin12), .pin18(DOut[7]), .pin17(DOut[6]), .pin16(DOut[5]),
    .pin15(DOut[4]), .pin14(DOut[3]), .pin13(DOut[2]), .pin12(DOut[1]), .pin11(DOut[0]));
  _74245 #(.ShowInternalStructure("true")) u_74245_6 (
    .pin1(n74245_6_pin1), .pin2(n74273_2_pin2[7]), .pin3(n74273_2_pin2[6]), .pin4(n74273_2_pin2[5]),
    .pin5(n74273_2_pin2[4]), .pin6(n74273_2_pin2[3]), .pin7(n74273_2_pin2[2]), .pin8(n74273_2_pin2[1]),
    .pin9(n74273_2_pin2[0]), .pin19(n7404_1_pin2), .pin18(DOut[7]), .pin17(DOut[6]), .pin16(DOut[5]),
    .pin15(DOut[4]), .pin14(DOut[3]), .pin13(DOut[2]), .pin12(DOut[1]), .pin11(DOut[0]));
  _74245 #(.ShowInternalStructure("true")) u_74245_7 (
    .pin1(n74245_7_pin1), .pin2(n74273_1_pin19[0]), .pin3(n74273_1_pin19[1]), .pin4(n74273_1_pin19[2]),
    .pin5(n74273_1_pin19[3]), .pin6(n74273_1_pin19[4]), .pin7(n74273_1_pin19[5]), .pin8(n74273_1_pin19[6]),
    .pin9(n74273_1_pin19[7]), .pin19(n7404_1_pin4), .pin18(D16Out[7]), .pin17(D16Out[6]), .pin16(D16Out[5]),
    .pin15(D16Out[4]), .pin14(D16Out[3]), .pin13(D16Out[2]), .pin12(D16Out[1]), .pin11(D16Out[0]));
  _74245 #(.ShowInternalStructure("true")) u_74245_8 (
    .pin1(n74245_8_pin1), .pin2(n74273_2_pin2[0]), .pin3(n74273_2_pin2[1]), .pin4(n74273_2_pin2[2]),
    .pin5(n74273_2_pin2[3]), .pin6(n74273_2_pin2[4]), .pin7(n74273_2_pin2[5]), .pin8(n74273_2_pin2[6]),
    .pin9(n74273_2_pin2[7]), .pin19(n7404_1_pin4), .pin18(D16Out[8]), .pin17(D16Out[9]), .pin16(D16Out[10]),
    .pin15(D16Out[11]), .pin14(D16Out[12]), .pin13(D16Out[13]), .pin12(D16Out[14]), .pin11(D16Out[15]));
  // also tied to VCC on the sheet: {n74245_1_pin1, n74245_2_pin1, n74245_3_pin1, n74245_4_pin1, n74245_5_pin1, n74245_6_pin1, n74245_7_pin1, n74245_8_pin1}
endmodule
module Input_register (
  input  CLK,
  input  Load,
  input  [7:0] Data_In,
  input  [23:0] SQC,
  input  En,
  output [7:0] Data_Out,
  output Reg_A,
  output Clock,
  output W
);

  wire n7404_1_pin2, n7404_1_pin6, n7404_1_pin10, n7404_1_pin12, n7408_1_pin2, n7408_1_pin3, n7408_1_pin5,
       n7432_1_pin3, n7432_1_pin11, n7432_2_pin2, n7432_2_pin3, n7432_2_pin5, n7432_2_pin6, n7432_2_pin8,
       n7432_2_pin9, n7432_2_pin11, n7432_2_pin12, n7432_3_pin1, n7432_3_pin3, n7432_3_pin11, n74245_1_pin1,
       n74273_1_pin2, n74273_1_pin5, n74273_1_pin6, n74273_1_pin9;
  wire [7:0] gate_8_1_dout;
  wire [23:0] pull_resistor_1_node;

  Pull_Resistor pull_resistor_1 (.node({pull_resistor_1_node[23:10], Reg_A, pull_resistor_1_node[8:0]}));
  _7432 #(.ShowInternalStructure("true")) u_7432_1 (
    .pin1(pull_resistor_1_node[10]), .pin2(Reg_A), .pin3(n7432_1_pin3), .pin4(n7432_1_pin3),
    .pin5(pull_resistor_1_node[8]), .pin6(Clock), .pin13(pull_resistor_1_node[12]),
    .pin12(pull_resistor_1_node[11]), .pin11(n7432_1_pin11));  // open: pin10, pin9, pin8
  GATE_24 gate_24_1 (.EN(En), .DIn(SQC), .DOut({pull_resistor_1_node[23:10], Reg_A, pull_resistor_1_node[8:0]}));
  _7404 #(.ShowInternalStructure("true")) u_7404_1 (
    .pin1(n7432_1_pin11), .pin2(n7404_1_pin2), .pin5(pull_resistor_1_node[5]), .pin6(n7404_1_pin6),
    .pin13(Clock), .pin12(n7404_1_pin12), .pin10(n7404_1_pin10));  // open: pin3, pin4, pin11, pin9, pin8
  _7408 #(.ShowInternalStructure("true")) u_7408_1 (
    .pin1(CLK), .pin2(n7408_1_pin2), .pin3(n7408_1_pin3), .pin4(pull_resistor_1_node[7]),
    .pin5(n7408_1_pin5), .pin6(W), .pin13(Load), .pin12(pull_resistor_1_node[6]), .pin11(n7408_1_pin2));  // open: pin10, pin9, pin8
  GATE_8 gate_8_1 (.EN(n7408_1_pin2), .DIn(Data_In), .DOut(gate_8_1_dout));
  _7432 #(.ShowInternalStructure("true")) u_7432_2 (
    .pin2(n7432_2_pin2), .pin3(n7432_2_pin3), .pin4(n7432_2_pin3), .pin5(n7432_2_pin5), .pin6(n7432_2_pin6),
    .pin13(n7432_2_pin6), .pin12(n7432_2_pin12), .pin11(n7432_2_pin11), .pin10(n7432_2_pin11),
    .pin9(n7432_2_pin9), .pin8(n7432_2_pin8));  // open: pin1
  _74273 #(.ShowInternalStructure("true")) u_74273_1 (
    .pin1(n7404_1_pin6), .pin2(n74273_1_pin2), .pin3(gate_8_1_dout[0]), .pin4(gate_8_1_dout[1]),
    .pin5(n74273_1_pin5), .pin6(n74273_1_pin6), .pin7(gate_8_1_dout[2]), .pin8(gate_8_1_dout[3]),
    .pin9(n74273_1_pin9), .pin19(n7432_2_pin2), .pin18(gate_8_1_dout[7]), .pin17(gate_8_1_dout[6]),
    .pin16(n7432_2_pin5), .pin15(n7432_2_pin9), .pin14(gate_8_1_dout[5]), .pin13(gate_8_1_dout[4]),
    .pin12(n7432_2_pin12), .pin11(n7408_1_pin3));
  _7432 #(.ShowInternalStructure("true")) u_7432_3 (
    .pin1(n7432_3_pin1), .pin2(n74273_1_pin6), .pin3(n7432_3_pin3), .pin4(n7432_3_pin3),
    .pin5(n74273_1_pin2), .pin6(n7408_1_pin5), .pin13(n7432_2_pin8), .pin12(n74273_1_pin9),
    .pin11(n7432_3_pin11), .pin10(n7432_3_pin11), .pin9(n74273_1_pin5), .pin8(n7432_3_pin1));
  _74245 #(.ShowInternalStructure("true")) u_74245_1 (
    .pin1(n74245_1_pin1), .pin2(n74273_1_pin2), .pin3(n74273_1_pin5), .pin4(n74273_1_pin6),
    .pin5(n74273_1_pin9), .pin6(n7432_2_pin12), .pin7(n7432_2_pin9), .pin8(n7432_2_pin5),
    .pin9(n7432_2_pin2), .pin19(n7404_1_pin12), .pin18(Data_Out[0]), .pin17(Data_Out[1]),
    .pin16(Data_Out[2]), .pin15(Data_Out[3]), .pin14(Data_Out[4]), .pin13(Data_Out[5]), .pin12(Data_Out[6]),
    .pin11(Data_Out[7]));
  // also tied to VCC on the sheet: n74245_1_pin1
endmodule

module MOV_16 (
  input  [7:0] Instructions,
  input  [23:0] SQC,
  output M_LOAD,
  output J_LOAD,
  output XY_LOAD,
  output J_SEL,
  output XY_SEL
);

  wire n7404_1_pin2, n7404_1_pin4, n7404_1_pin6, n7404_1_pin12, n7408_1_pin3, n7408_1_pin4, n7408_1_pin5,
       n7408_1_pin6, n7408_1_pin8, n7408_1_pin11, n7408_2_pin1, n7408_2_pin3, n7408_2_pin6, n7408_2_pin11,
       n7408_3_pin3, n7432_1_pin3, n7432_1_pin6;

  _7432 #(.ShowInternalStructure("true")) u_7432_1 (
    .pin1(SQC[7]), .pin2(SQC[6]), .pin3(n7432_1_pin3), .pin4(n7432_1_pin3), .pin5(SQC[5]), .pin6(n7432_1_pin6));  // open: pin13, pin12, pin11, pin10, pin9, pin8
  _7408 #(.ShowInternalStructure("true")) u_7408_1 (
    .pin1(n7432_1_pin6), .pin2(Instructions[2]), .pin3(n7408_1_pin3), .pin4(n7408_1_pin4),
    .pin5(n7408_1_pin5), .pin6(n7408_1_pin6), .pin13(SQC[6]), .pin12(Instructions[1]), .pin11(n7408_1_pin11),
    .pin10(SQC[6]), .pin9(Instructions[0]), .pin8(n7408_1_pin8));
  _7404 #(.ShowInternalStructure("true")) u_7404_1 (
    .pin1(Instructions[6]), .pin2(n7404_1_pin2), .pin3(Instructions[4]), .pin4(n7404_1_pin4),
    .pin5(Instructions[3]), .pin6(n7404_1_pin6), .pin13(n7408_1_pin3), .pin12(n7404_1_pin12),
    .pin11(n7408_1_pin11), .pin10(n7408_1_pin4), .pin9(n7408_1_pin8), .pin8(n7408_1_pin5));
  _7408 #(.ShowInternalStructure("true")) u_7408_2 (
    .pin1(n7408_2_pin1), .pin2(Instructions[7]), .pin3(n7408_2_pin3), .pin4(n7408_2_pin3),
    .pin5(Instructions[5]), .pin6(n7408_2_pin6), .pin13(n7404_1_pin2), .pin12(n7404_1_pin4),
    .pin11(n7408_2_pin11), .pin10(n7408_2_pin11), .pin9(n7404_1_pin6), .pin8(n7408_2_pin1));
  _7408 #(.ShowInternalStructure("true")) u_7408_3 (
    .pin1(n7408_2_pin6), .pin2(n7432_1_pin6), .pin3(n7408_3_pin3));  // open: pin4, pin5, pin6, pin13, pin12, pin11, pin10, pin9, pin8
  _7408 #(.ShowInternalStructure("true")) u_7408_4 (
    .pin4(n7408_1_pin11), .pin5(n7408_3_pin3), .pin6(M_LOAD));  // open: pin1, pin2, pin3, pin13, pin12, pin11, pin10, pin9, pin8
  _7408 #(.ShowInternalStructure("true")) u_7408_5 (
    .pin1(n7408_3_pin3), .pin2(n7408_1_pin8), .pin3(J_LOAD), .pin4(n7408_3_pin3), .pin5(n7404_1_pin12),
    .pin6(XY_SEL), .pin13(n7408_3_pin3), .pin12(n7408_1_pin6), .pin11(XY_LOAD), .pin10(n7408_3_pin3),
    .pin9(n7408_1_pin3), .pin8(J_SEL));
endmodule

module SRL_OUT (
  input  [7:0] DATA,
  input  ENABLE,
  input  CLK,
  input  [23:0] SQC,
  output Serial_Out_XOR,
  output Serial_out,
  output Resume,
  output A_SELECT
);

  wire n7404_1_pin2, n7404_1_pin4, n7404_1_pin6, n7404_1_pin8, n7404_1_pin10, n7404_1_pin12, n7404_2_pin10,
       n7404_2_pin12, n7404_3_pin2, n7404_3_pin4, n7404_3_pin6, n7404_3_pin10, n7408_1_pin3, n7408_1_pin5,
       n7408_1_pin11, n7408_1_pin13, n7408_2_pin3, n7408_2_pin6, n7408_2_pin8, n7408_2_pin11, n7408_3_pin3,
       n7408_3_pin6, n7408_4_pin3, n7408_4_pin6, n7408_4_pin8, n7432_1_pin3, n7432_1_pin6, n7432_1_pin8,
       n7432_1_pin11, n7432_2_pin9, n74165_1_pin9, n74165_1_pin15, n74192_1_pin3, n74192_1_pin4,
       n74192_1_pin6, n74192_1_pin7, n74273_1_pin11;
  wire [7:0] n74273_1_pin2;

  _7404 #(.ShowInternalStructure("true")) u_7404_1 (
    .pin1(SQC[5]), .pin2(n7404_1_pin2), .pin3(SQC[4]), .pin4(n7404_1_pin4), .pin5(SQC[3]),
    .pin6(n7404_1_pin6), .pin13(SQC[0]), .pin12(n7404_1_pin12), .pin11(SQC[1]), .pin10(n7404_1_pin10),
    .pin9(SQC[2]), .pin8(n7404_1_pin8));
  _7404 #(.ShowInternalStructure("true")) u_7404_2 (
    .pin13(SQC[7]), .pin12(n7404_2_pin12), .pin11(SQC[6]), .pin10(n7404_2_pin10));  // open: pin1, pin2, pin3, pin4, pin5, pin6, pin9, pin8
  _7408 #(.ShowInternalStructure("true")) u_7408_1 (
    .pin1(ENABLE), .pin2(CLK), .pin3(n7408_1_pin3), .pin4(ENABLE), .pin5(n7408_1_pin5),
    .pin13(n7408_1_pin13), .pin12(n7408_1_pin3), .pin11(n7408_1_pin11));  // open: pin6, pin10, pin9, pin8
  _74192 #(.ShowInternalStructure("true")) u_74192_1 (
    .pin2(n7408_1_pin5), .pin3(n74192_1_pin3), .pin4(n74192_1_pin4), .pin5(n7408_1_pin11),
    .pin6(n74192_1_pin6), .pin7(n74192_1_pin7), .pin12(Resume), .pin11(n74192_1_pin4));  // open: pin1, pin15, pin14, pin13, pin10, pin9
  _7432 #(.ShowInternalStructure("true")) u_7432_1 (
    .pin1(n74192_1_pin3), .pin2(n7408_1_pin5), .pin3(n7432_1_pin3), .pin4(n7432_1_pin3), .pin6(n7432_1_pin6),
    .pin13(n7432_1_pin6), .pin12(n74192_1_pin6), .pin11(n7432_1_pin11), .pin10(n7432_1_pin11),
    .pin9(n74192_1_pin7), .pin8(n7432_1_pin8));  // open: pin5
  _7408 #(.ShowInternalStructure("true")) u_7408_2 (
    .pin1(n7404_1_pin12), .pin2(n7404_1_pin10), .pin3(n7408_2_pin3), .pin4(n7404_1_pin8),
    .pin5(n7404_1_pin6), .pin6(n7408_2_pin6), .pin13(n7404_1_pin4), .pin12(n7404_1_pin2),
    .pin11(n7408_2_pin11), .pin10(n7404_2_pin10), .pin9(n7404_2_pin12), .pin8(n7408_2_pin8));
  _74273 #(.ShowInternalStructure("true")) u_74273_1 (
    .pin2(n74273_1_pin2[0]), .pin3(DATA[0]), .pin4(DATA[1]), .pin5(n74273_1_pin2[1]),
    .pin6(n74273_1_pin2[2]), .pin7(DATA[2]), .pin8(DATA[3]), .pin9(n74273_1_pin2[3]),
    .pin19(n74273_1_pin2[7]), .pin18(DATA[7]), .pin17(DATA[6]), .pin16(n74273_1_pin2[6]),
    .pin15(n74273_1_pin2[5]), .pin14(DATA[5]), .pin13(DATA[4]), .pin12(n74273_1_pin2[4]),
    .pin11(n74273_1_pin11));  // open: pin1
  _7404 #(.ShowInternalStructure("true")) u_7404_3 (
    .pin1(n7408_1_pin5), .pin2(n7404_3_pin2), .pin3(n74192_1_pin3), .pin4(n7404_3_pin4),
    .pin5(n74192_1_pin7), .pin6(n7404_3_pin6), .pin13(n74192_1_pin7), .pin11(n74192_1_pin6),
    .pin10(n7404_3_pin10), .pin9(n7432_1_pin8));  // open: pin12, pin8
  _74165 #(.ShowInternalStructure("true")) u_74165_1 (
    .pin1(n7432_1_pin8), .pin2(CLK), .pin3(n74273_1_pin2[4]), .pin4(n74273_1_pin2[5]),
    .pin5(n74273_1_pin2[6]), .pin6(n74273_1_pin2[7]), .pin15(n74165_1_pin15), .pin14(n74273_1_pin2[3]),
    .pin13(n74273_1_pin2[2]), .pin12(n74273_1_pin2[1]), .pin11(n74273_1_pin2[0]), .pin9(n74165_1_pin9));  // open: pin7, pin10
  _7408 #(.ShowInternalStructure("true")) u_7408_3 (
    .pin1(n7408_2_pin3), .pin2(n7408_2_pin11), .pin3(n7408_3_pin3), .pin4(n7408_2_pin6), .pin5(n7408_2_pin8),
    .pin6(n7408_3_pin6), .pin10(n7408_3_pin3), .pin9(n7408_3_pin6), .pin8(n7408_1_pin13));  // open: pin13, pin12, pin11
  _7432 #(.ShowInternalStructure("true")) u_7432_2 (
    .pin10(A_SELECT), .pin9(n7432_2_pin9), .pin8(n74273_1_pin11));  // open: pin1, pin2, pin3, pin4, pin5, pin6, pin13, pin12, pin11
  _7408 #(.ShowInternalStructure("true")) u_7408_4 (
    .pin1(n7404_3_pin2), .pin2(n74192_1_pin3), .pin3(n7408_4_pin3), .pin4(n7404_3_pin10),
    .pin5(n7404_3_pin6), .pin6(n7408_4_pin6), .pin13(n7408_4_pin3), .pin12(n7408_4_pin6), .pin11(A_SELECT),
    .pin10(n7404_3_pin4), .pin9(n7408_4_pin6), .pin8(n7408_4_pin8));
  _7486 #(.ShowInternalStructure("true")) u_7486_1 (
    .pin1(n7408_1_pin11), .pin2(Serial_out), .pin3(Serial_Out_XOR), .pin4(Serial_Out_XOR));  // open: pin5, pin6, pin13, pin12, pin11, pin10, pin9, pin8
  _7408 #(.ShowInternalStructure("true")) u_7408_5 (
    .pin1(n7408_4_pin8), .pin2(n7408_1_pin5), .pin3(n7432_2_pin9), .pin12(n74165_1_pin9), .pin11(Serial_out));  // open: pin4, pin5, pin6, pin13, pin10, pin9, pin8
  // also tied to GND on the sheet: n74165_1_pin15
  // also tied to VCC on the sheet: n74192_1_pin4
endmodule

module GATE_8_ALU (
  input  EN,
  input  [7:0] DIn,
  output [7:0] DOut
);

  wire n7404_1_pin6, n74245_1_pin1;

  Pull_Resistor pull_resistor_1 (.node(DIn));
  _7404 #(.ShowInternalStructure("true")) u_7404_1 (
    .pin5(EN), .pin6(n7404_1_pin6));  // open: pin1, pin2, pin3, pin4, pin13, pin12, pin11, pin10, pin9, pin8
  _74245 #(.ShowInternalStructure("true")) u_74245_1 (
    .pin1(n74245_1_pin1), .pin2(DIn[0]), .pin3(DIn[1]), .pin4(DIn[2]), .pin5(DIn[3]), .pin6(DIn[4]),
    .pin7(DIn[5]), .pin8(DIn[6]), .pin9(DIn[7]), .pin19(n7404_1_pin6), .pin18(DOut[0]), .pin17(DOut[1]),
    .pin16(DOut[2]), .pin15(DOut[3]), .pin14(DOut[4]), .pin13(DOut[5]), .pin12(DOut[6]), .pin11(DOut[7]));
  // also tied to VCC on the sheet: n74245_1_pin1
endmodule

module STATUS_CHECK (
  input  [23:0] SQC,
  input  [7:0] INSTR,
  output FREE
);

  wire n7404_1_pin2, n7404_1_pin4, n7404_1_pin6, n7404_1_pin8, n7404_1_pin10, n7404_1_pin12, n7404_2_pin10,
       n7404_2_pin12, n7404_3_pin2, n7404_3_pin4, n7404_3_pin6, n7404_3_pin8, n7404_3_pin10, n7404_3_pin12,
       n7404_4_pin2, n7404_4_pin4, n7404_4_pin6, n7404_4_pin8, n7404_4_pin10, n7404_4_pin12, n7404_5_pin2,
       n7404_5_pin4, n7404_5_pin6, n7404_5_pin8, n7404_5_pin10, n7404_5_pin12, n7404_6_pin2, n7404_6_pin4,
       n7404_6_pin6, n7404_6_pin8, n7404_6_pin10, n7404_6_pin12, n7408_1_pin3, n7408_1_pin6, n7408_1_pin8,
       n7408_1_pin11, n7408_2_pin3, n7408_2_pin6, n7408_2_pin8, n7408_2_pin11, n7408_3_pin3, n7408_3_pin6,
       n7408_3_pin8, n7408_3_pin11, n7408_4_pin3, n7408_4_pin6, n7408_4_pin8, n7408_4_pin11, n7408_5_pin3,
       n7408_5_pin6, n7408_5_pin8, n7408_5_pin11, n7408_6_pin3, n7408_6_pin5, n7408_6_pin6, n7408_6_pin10,
       n7408_7_pin3, n7408_8_pin3, n7408_8_pin11, n7408_9_pin3, n7408_9_pin11, n7408_10_pin3;

  _7404 #(.ShowInternalStructure("true")) u_7404_1 (
    .pin1(INSTR[7]), .pin2(n7404_1_pin2), .pin3(INSTR[6]), .pin4(n7404_1_pin4), .pin5(INSTR[3]),
    .pin6(n7404_1_pin6), .pin13(INSTR[0]), .pin12(n7404_1_pin12), .pin11(INSTR[1]), .pin10(n7404_1_pin10),
    .pin9(INSTR[2]), .pin8(n7404_1_pin8));
  _7404 #(.ShowInternalStructure("true")) u_7404_2 (
    .pin13(INSTR[5]), .pin12(n7404_2_pin12), .pin11(INSTR[4]), .pin10(n7404_2_pin10));  // open: pin1, pin2, pin3, pin4, pin5, pin6, pin9, pin8
  _7404 #(.ShowInternalStructure("true")) u_7404_3 (
    .pin1(SQC[3]), .pin2(n7404_3_pin2), .pin3(SQC[4]), .pin4(n7404_3_pin4), .pin5(SQC[5]),
    .pin6(n7404_3_pin6), .pin13(SQC[0]), .pin12(n7404_3_pin12), .pin11(SQC[1]), .pin10(n7404_3_pin10),
    .pin9(SQC[2]), .pin8(n7404_3_pin8));
  _7404 #(.ShowInternalStructure("true")) u_7404_4 (
    .pin1(SQC[10]), .pin2(n7404_4_pin2), .pin3(SQC[11]), .pin4(n7404_4_pin4), .pin5(SQC[12]),
    .pin6(n7404_4_pin6), .pin13(SQC[9]), .pin12(n7404_4_pin12), .pin11(SQC[8]), .pin10(n7404_4_pin10),
    .pin9(SQC[7]), .pin8(n7404_4_pin8));
  _7404 #(.ShowInternalStructure("true")) u_7404_5 (
    .pin1(SQC[18]), .pin2(n7404_5_pin2), .pin3(SQC[17]), .pin4(n7404_5_pin4), .pin5(SQC[16]),
    .pin6(n7404_5_pin6), .pin13(SQC[15]), .pin12(n7404_5_pin12), .pin11(SQC[14]), .pin10(n7404_5_pin10),
    .pin9(SQC[13]), .pin8(n7404_5_pin8));
  _7404 #(.ShowInternalStructure("true")) u_7404_6 (
    .pin1(SQC[22]), .pin2(n7404_6_pin2), .pin3(SQC[23]), .pin4(n7404_6_pin4), .pin5(SQC[6]),
    .pin6(n7404_6_pin6), .pin13(SQC[21]), .pin12(n7404_6_pin12), .pin11(SQC[20]), .pin10(n7404_6_pin10),
    .pin9(SQC[19]), .pin8(n7404_6_pin8));
  _7408 #(.ShowInternalStructure("true")) u_7408_1 (
    .pin1(n7404_2_pin12), .pin2(n7404_2_pin10), .pin3(n7408_1_pin3), .pin4(n7404_1_pin2),
    .pin5(n7404_1_pin4), .pin6(n7408_1_pin6), .pin13(n7404_1_pin8), .pin12(n7404_1_pin10),
    .pin11(n7408_1_pin11), .pin10(n7404_1_pin12), .pin9(n7404_1_pin6), .pin8(n7408_1_pin8));
  _7408 #(.ShowInternalStructure("true")) u_7408_2 (
    .pin1(n7404_3_pin6), .pin2(n7404_3_pin4), .pin3(n7408_2_pin3), .pin4(n7404_3_pin10),
    .pin5(n7404_3_pin12), .pin6(n7408_2_pin6), .pin13(n7404_3_pin8), .pin12(n7404_3_pin2),
    .pin11(n7408_2_pin11), .pin10(n7408_2_pin11), .pin9(n7408_2_pin6), .pin8(n7408_2_pin8));
  _7408 #(.ShowInternalStructure("true")) u_7408_3 (
    .pin1(n7404_4_pin6), .pin2(n7404_4_pin4), .pin3(n7408_3_pin3), .pin4(n7404_4_pin12), .pin5(n7404_4_pin2),
    .pin6(n7408_3_pin6), .pin13(n7404_4_pin10), .pin12(n7404_4_pin8), .pin11(n7408_3_pin11),
    .pin10(n7408_3_pin11), .pin9(n7408_3_pin6), .pin8(n7408_3_pin8));
  _7408 #(.ShowInternalStructure("true")) u_7408_4 (
    .pin1(n7404_5_pin6), .pin2(n7404_5_pin4), .pin3(n7408_4_pin3), .pin4(n7404_5_pin12), .pin5(n7404_5_pin2),
    .pin6(n7408_4_pin6), .pin13(n7404_5_pin8), .pin12(n7404_5_pin10), .pin11(n7408_4_pin11),
    .pin10(n7408_4_pin11), .pin9(n7408_4_pin6), .pin8(n7408_4_pin8));
  _7408 #(.ShowInternalStructure("true")) u_7408_5 (
    .pin1(n7404_6_pin6), .pin2(n7404_6_pin4), .pin3(n7408_5_pin3), .pin4(n7404_6_pin12), .pin5(n7404_6_pin2),
    .pin6(n7408_5_pin6), .pin13(n7404_6_pin8), .pin12(n7404_6_pin10), .pin11(n7408_5_pin11),
    .pin10(n7408_5_pin11), .pin9(n7408_5_pin6), .pin8(n7408_5_pin8));
  _7408 #(.ShowInternalStructure("true")) u_7408_6 (
    .pin1(n7408_1_pin6), .pin2(n7408_1_pin3), .pin3(n7408_6_pin3), .pin4(n7408_6_pin3), .pin5(n7408_6_pin5),
    .pin6(n7408_6_pin6), .pin13(n7408_1_pin8), .pin12(n7408_1_pin11), .pin11(n7408_6_pin5),
    .pin10(n7408_6_pin10), .pin9(n7408_6_pin6), .pin8(FREE));
  _7408 #(.ShowInternalStructure("true")) u_7408_7 (
    .pin1(n7408_2_pin8), .pin2(n7408_2_pin3), .pin3(n7408_7_pin3));  // open: pin4, pin5, pin6, pin13, pin12, pin11, pin10, pin9, pin8
  _7408 #(.ShowInternalStructure("true")) u_7408_8 (
    .pin1(n7408_3_pin8), .pin2(n7408_3_pin3), .pin3(n7408_8_pin3), .pin13(n7408_7_pin3),
    .pin12(n7408_8_pin3), .pin11(n7408_8_pin11));  // open: pin4, pin5, pin6, pin10, pin9, pin8
  _7408 #(.ShowInternalStructure("true")) u_7408_9 (
    .pin1(n7408_4_pin8), .pin2(n7408_4_pin3), .pin3(n7408_9_pin3), .pin13(n7408_9_pin3),
    .pin12(n7408_8_pin11), .pin11(n7408_9_pin11));  // open: pin4, pin5, pin6, pin10, pin9, pin8
  _7408 #(.ShowInternalStructure("true")) u_7408_10 (
    .pin1(n7408_5_pin8), .pin2(n7408_5_pin3), .pin3(n7408_10_pin3), .pin13(n7408_10_pin3),
    .pin12(n7408_9_pin11), .pin11(n7408_6_pin10));  // open: pin4, pin5, pin6, pin10, pin9, pin8
endmodule

module SCHEDULER (
  input  CPU_A_FREE,
  input  CPU_B_FREE,
  input  CPU_C_FREE,
  input  CPU_D_FREE
);
endmodule

module BUS_ARBITER (
  input  CLK,
  input  REQ_A,
  input  REQ_B,
  output GRANT_A,
  output GRANT_B,
  output EN_A,
  output EN_B,
  output O
);

  wire AND3, ENA_C, ENB_C, HI, nCLK, nGB, nO, nREQ_A, nREQ_B, ONEXT, ORa, ORb;

  _7404 #(.ShowInternalStructure("true")) u_7404_1 (
    .pin1(REQ_A), .pin2(nREQ_A), .pin3(REQ_B), .pin4(nREQ_B), .pin5(O), .pin6(nO), .pin11(CLK), .pin10(nCLK),
    .pin9(GRANT_B), .pin8(nGB));  // open: pin13, pin12
  _7432 #(.ShowInternalStructure("true")) u_7432_1 (
    .pin1(nREQ_B), .pin2(O), .pin3(ORa), .pin4(nREQ_A), .pin5(nO), .pin6(ORb), .pin13(nREQ_A),
    .pin12(GRANT_A), .pin11(ENA_C), .pin10(AND3), .pin9(GRANT_A), .pin8(ONEXT));
  _7432 #(.ShowInternalStructure("true")) u_7432_2 (
    .pin1(GRANT_B), .pin2(nREQ_B), .pin3(ENB_C));  // open: pin4, pin5, pin6, pin13, pin12, pin11, pin10, pin9, pin8
  _7408 #(.ShowInternalStructure("true")) u_7408_1 (
    .pin1(REQ_A), .pin2(ORa), .pin3(GRANT_A), .pin4(REQ_B), .pin5(ORb), .pin6(GRANT_B), .pin10(nGB),
    .pin9(O), .pin8(AND3));  // open: pin13, pin12, pin11
  _7474 #(.ShowInternalStructure("true")) u_7474_1 (
    .pin1(HI), .pin2(ONEXT), .pin3(CLK), .pin4(HI), .pin5(O), .pin13(HI), .pin12(ENA_C), .pin11(nCLK),
    .pin10(HI), .pin9(EN_A));  // open: pin6, pin8
  _7474 #(.ShowInternalStructure("true")) u_7474_2 (
    .pin1(HI), .pin2(ENB_C), .pin3(nCLK), .pin4(HI), .pin5(EN_B), .pin13(HI), .pin10(HI));  // open: pin6, pin12, pin11, pin9, pin8
  // also tied to VCC on the sheet: HI

  // Other names for the same wires on the sheet: ENA_L = EN_A; ENB_L = EN_B; GA = GRANT_A; GB = GRANT_B
endmodule

module CPU_SHARED (
  input  CPU_ENABLE,
  input  [7:0] Data_In,
  input  EN,
  input  GRANT,
  input  FORK_LOAD,
  input  [15:0] FORK_ADDR_IN,
  input  [7:0] CPU_ID,
  output [23:0] Sequnce,
  output FREE,
  output [15:0] Adress_Bus,
  output Write_en,
  output [7:0] Data_Out,
  output BUS_REQ,
  output FORK_REQ,
  output [15:0] FORK_ADDR
);

  wire CPUEN_INT, HI, nGRANT, WE_N;
  wire [7:0] DOUT_N;

  _7408 #(.ShowInternalStructure("true")) u_7408_1 (
    .pin1(CPU_ENABLE), .pin2(EN), .pin3(CPUEN_INT));  // open: pin4, pin5, pin6, pin13, pin12, pin11, pin10, pin9, pin8
  CPU cpu_1 (
    .CPU_ENABLE(CPUEN_INT), .Data_In(Data_In), .FORK_LOAD(FORK_LOAD), .FORK_ADDR_IN(FORK_ADDR_IN),
    .CPU_ID(CPU_ID), .Sequnce(Sequnce), .FREE(FREE), .Adress_Bus(FORK_ADDR), .Write_en(WE_N),
    .Data_Out(DOUT_N), .BUS_REQ(BUS_REQ), .FORK_REQ(FORK_REQ));
  _7404 #(.ShowInternalStructure("true")) u_7404_1 (
    .pin1(GRANT), .pin2(nGRANT));  // open: pin3, pin4, pin5, pin6, pin13, pin12, pin11, pin10, pin9, pin8
  _74245 #(.ShowInternalStructure("true")) u_74245_1 (
    .pin1(HI), .pin2(WE_N), .pin19(nGRANT), .pin18(Write_en));  // open: pin3, pin4, pin5, pin6, pin7, pin8, pin9, pin17, pin16, pin15, pin14, pin13, pin12, pin11
  Pull_Resistor pull_resistor_1 (.node(Write_en));
  GATE_8_ALU gate_8_alu_1 (.EN(GRANT), .DIn(FORK_ADDR[7:0]), .DOut(Adress_Bus[7:0]));
  GATE_8_ALU gate_8_alu_2 (.EN(GRANT), .DIn(FORK_ADDR[15:8]), .DOut(Adress_Bus[15:8]));
  GATE_8_ALU gate_8_alu_3 (.EN(GRANT), .DIn(DOUT_N), .DOut(Data_Out));
  // also tied to VCC on the sheet: HI

  // Other names for the same wires on the sheet: ADDR16[15:0] = FORK_ADDR; ALO[7:0] = FORK_ADDR[7:0];
  //   AHI[7:0] = FORK_ADDR[15:8]; ADDR_OUT[15:0] = Adress_Bus; ALO_G[7:0] = Adress_Bus[7:0];
  //   AHI_G[7:0] = Adress_Bus[15:8]; DOUT_OUT[7:0] = Data_Out; FORK_REQ_N = FORK_REQ; FREE_N = FREE; REQ_N = BUS_REQ;
  //   SEQ[23:0] = Sequnce; WE_OUT = Write_en
endmodule

module FORKUNIT (
  input  [7:0] INSTR,
  input  [23:0] SQC,
  output NEWOP,
  output ID_ALOAD,
  output ID_OE,
  output FORK_REQ,
  output FORK_MSEL
);

  wire CPUID, FORK, nb0, nb5, nb6, sx, ta, tb, tc, td, te, W;

  _7404 #(.ShowInternalStructure("true")) u_7404_1 (
    .pin1(INSTR[6]), .pin2(nb6), .pin3(INSTR[5]), .pin4(nb5), .pin5(INSTR[0]), .pin6(nb0));  // open: pin13, pin12, pin11, pin10, pin9, pin8
  _7408 #(.ShowInternalStructure("true")) u_7408_1 (
    .pin1(INSTR[7]), .pin2(nb6), .pin3(ta), .pin4(nb5), .pin5(INSTR[4]), .pin6(tb), .pin13(tb), .pin12(ta),
    .pin11(td), .pin10(INSTR[2]), .pin9(INSTR[3]), .pin8(tc));
  _7408 #(.ShowInternalStructure("true")) u_7408_2 (
    .pin1(tc), .pin2(INSTR[1]), .pin3(te), .pin4(td), .pin5(te), .pin6(NEWOP), .pin13(INSTR[0]),
    .pin12(NEWOP), .pin11(FORK), .pin10(nb0), .pin9(NEWOP), .pin8(CPUID));
  _7432 #(.ShowInternalStructure("true")) u_7432_1 (
    .pin1(SQC[7]), .pin2(SQC[8]), .pin3(sx), .pin4(sx), .pin5(SQC[9]), .pin6(W));  // open: pin13, pin12, pin11, pin10, pin9, pin8
  _7408 #(.ShowInternalStructure("true")) u_7408_3 (
    .pin1(CPUID), .pin2(W), .pin3(ID_OE), .pin4(CPUID), .pin5(SQC[8]), .pin6(ID_ALOAD), .pin13(W),
    .pin12(FORK), .pin11(FORK_MSEL), .pin10(SQC[8]), .pin9(FORK), .pin8(FORK_REQ));

  // Other names for the same wires on the sheet: FMS = FORK_MSEL; FRQ = FORK_REQ; IDA = ID_ALOAD; IDO = ID_OE;
  //   b0 = INSTR[0]; b1 = INSTR[1]; b2 = INSTR[2]; b3 = INSTR[3]; b4 = INSTR[4]; b5 = INSTR[5]; b6 = INSTR[6];
  //   b7 = INSTR[7]; s7 = SQC[7]; s8 = SQC[8]; s9 = SQC[9]; T = NEWOP
endmodule
